// Logisim project hw2part2.circ as structural Verilog: 1 circuit, main circuit main
module main (
  input  MuxCSel,
  input  [1:0] FunSel2a,
  input  [1:0] OutASel,
  input  [1:0] OutBSel,
  input  [3:0] FunSelALU,
  input  [3:0] RegSel2a,
  input  [1:0] MuxASel,
  input  [1:0] FunSel2b,
  input  [1:0] OutCSel,
  input  [1:0] MuxBSel,
  input  [1:0] OutDSel,
  input  strMEM,
  input  selMEM,
  input  ldMEM,
  input  clrMEM,
  input  [2:0] RegSel2b,
  input  [1:0] FunSel2c,
  input  nL_H,
  input  E2c,
  output [3:0] ZCNO_Register,
  output [15:0] IR
);

  wire clock_1_out;
  wire [3:0] alu_1_outflag;
  wire [7:0] alu_1_outalu, multiplexer_1_out, multiplexer_2_out, multiplexer_3_out, part2a_outa, part2a_outb,
       part2b_outc, part2b_outd, ram_1_data, undriven;

  Multiplexer #(.select(2), .width(8), .enable("false")) multiplexer_1 (
    .in0(IR[7:0]), .in1(ram_1_data), .in2(part2b_outc), .in3(alu_1_outalu), .out(multiplexer_1_out),
    .sel(MuxASel));
  part2a_main part2a (
    .INPUT(multiplexer_1_out), .OutA(part2a_outa), .OutB(part2a_outb), .RegSel(RegSel2a), .FunSel(FunSel2a),
    .OutASel(OutASel), .OutBSel(OutBSel));
  part2c_main part2c (.out_5(IR), .FunSel(FunSel2c), .EN(E2c), .in_3(ram_1_data), .nL_H(nL_H));
  Multiplexer #(.width(8), .enable("false")) multiplexer_2 (
    .in0(multiplexer_1_out), .in1(part2a_outa), .out(multiplexer_2_out), .sel(MuxCSel));
  Multiplexer #(.select(2), .width(8), .enable("false")) multiplexer_3 (
    .in0(undriven), .in1(IR[7:0]), .in2(ram_1_data), .in3(alu_1_outalu), .out(multiplexer_3_out),
    .sel(MuxBSel));
  ALU alu_1 (
    .FunSel(FunSelALU), .A(multiplexer_2_out), .B(part2a_outb), .OutALU(alu_1_outalu),
    .OutFlag(alu_1_outflag), .Cin(ZCNO_Register[0]));
  part2b_main part2b (
    .INPUT(multiplexer_3_out), .OutC(part2b_outc), .OutD(part2b_outd), .RegSel(RegSel2b), .FunSel(FunSel2b),
    .OutCSel(OutCSel), .OutDSel(OutDSel));
  register Flag_Register (.CLK(clock_1_out), .out_3(ZCNO_Register), .in_2(alu_1_outflag));
  RAM #(.bus("separate")) ram_1 (
    .addr(part2b_outd), .din(alu_1_outalu), .data(ram_1_data), .str(strMEM), .sel(selMEM), .clk(clock_1_out),
    .ld(ldMEM), .clr(clrMEM));
  Clock clock_1 (.out(clock_1_out));

  // Notes on the sheet:
  //   OutALU
endmodule
