// Logisim project hw3.circ as structural Verilog: 2 circuits, main circuit main
module main (
  input  [15:0] IR,
  output TYPE_2_INSTR,
  output TYPE_1_INSTR
);

  wire _1MSB, _2MSB, ADD__MOD, and_2_out, and_3_out, and_4_out, and_6_out, and_7_out, and_8_out, and_9_out,
       and_10_out, and_11_out, and_13_out, and_14_out, and_15_out, and_16_out, and_17_out, and_18_out,
       and_19_out, and_20_out, and_21_out, and_23_out, and_24_out, and_25_out, and_26_out, and_28_out,
       and_29_out, and_30_out, and_31_out, and_32_out, and_33_out, and_35_out, and_36_out, and_37_out,
       and_39_out, and_40_out, and_42_out, and_43_out, and_45_out, and_46_out, and_47_out, and_48_out,
       and_49_out, and_50_out, and_51_out, and_52_out, and_53_out, and_54_out, and_55_out, and_56_out,
       and_57_out, and_58_out, and_59_out, and_60_out, and_61_out, and_62_out, and_63_out, and_64_out,
       and_65_out, and_66_out, and_67_out, and_68_out, and_69_out, and_70_out, and_71_out, and_72_out,
       and_73_out, and_74_out, and_75_out, and_76_out, and_77_out, and_78_out, and_80_out, C, clrMEM, D0, D1,
       D2, D3, D4, D5, D6, D7, D8, D9, D_S, Da, Db, Dc, Dd, De, Df, Dg, Dh, Di, Enable2c, ldMEM, MuxCSel, N,
       nL_H, not_1_out, not_2_out, not_3_out, not_5_out, not_6_out, not_7_out, not_8_out, not_9_out,
       not_10_out, not_11_out, not_12_out, not_13_out, not_14_out, not_15_out, not_16_out, not_17_out,
       not_18_out, not_19_out, not_20_out, not_21_out, not_22_out, not_23_out, not_24_out, not_25_out,
       not_27_out, not_28_out, not_29_out, not_30_out, not_31_out, not_32_out, not_33_out, O, or_1_out,
       or_2_out, or_4_out, or_5_out, or_7_out, or_8_out, or_9_out, or_10_out, or_11_out, or_12_out,
       or_13_out, or_14_out, or_15_out, or_16_out, or_17_out, or_19_out, or_20_out, or_21_out, or_22_out,
       or_23_out, or_24_out, or_25_out, Res0, Res1, Res3, Res4, Res7_8, Res_efg, ResALU1, ResALU2, Reset,
       ResetBonus, Resh, Resi, selMEM, strMEM, T0, T1, T2, T3, T4, T5, T6, T7, Z;
  wire [1:0] _1SEL, _2SEL, ADDRESS, FunSel2a, FunSel2b, FunSel2c, multiplexer_3_out, multiplexer_9_out,
       multiplexer_15_out, multiplexer_16_out, multiplexer_18_out, multiplexer_21_out, multiplexer_22_out,
       MuxASel, MuxBSel, OutASel, OutBSel, OutCSel, OutDSel;
  wire [2:0] multiplexer_1_out, multiplexer_5_out, multiplexer_7_out, multiplexer_10_out, multiplexer_13_out,
       multiplexer_17_out, multiplexer_20_out, RegSel2b, xor_1_out;
  wire [2:1] DESTREG;
  wire [3:0] ALUFunSelCh, decoder_1_out0, decoder_2_out0, FunSelALU, multiplexer_2_out, multiplexer_4_out,
       multiplexer_6_out, multiplexer_11_out, multiplexer_12_out, multiplexer_14_out, multiplexer_19_out,
       multiplexer_23_out, RegSel2a;
  wire [15:11] IR_t;

  not not_1 (not_1_out, ADD__MOD);
  seq_counter seq_counter_1 (.RESET(Reset), .T0(T0), .T1(T1), .T2(T2), .T3(T3), .T4(T4), .T5(T5), .T6(T6), .T7(T7));
  and and_1 (Res0, D0, T4);
  Decoder #(.select(2), .enable("false")) decoder_1 (
    .out0(decoder_1_out0[0]), .out1(decoder_1_out0[1]), .out2(decoder_1_out0[2]), .out3(decoder_1_out0[3]),
    .sel(DESTREG));
  Decoder #(.select(2), .enable("false")) decoder_2 (
    .out0(decoder_2_out0[0]), .out1(decoder_2_out0[1]), .out2(decoder_2_out0[2]), .out3(decoder_2_out0[3]),
    .sel(DESTREG));
  and and_2 (and_2_out, D0, T3);
  and and_3 (and_3_out, not_1_out, and_2_out);
  assign MuxASel = and_3_out ? 2'b00 : 2'bz;  // Controlled_Buffer controlled_buffer_1
  assign FunSel2a = and_3_out ? 2'b01 : 2'bz;  // Controlled_Buffer controlled_buffer_2
  assign RegSel2a = and_3_out ? decoder_1_out0 : 4'bz;  // Controlled_Buffer controlled_buffer_3
  and and_4 (and_4_out, ADD__MOD, and_2_out);
  assign OutDSel = and_4_out ? 2'b01 : 2'bz;  // Controlled_Buffer controlled_buffer_4
  assign ldMEM = and_4_out ? 1'b1 : 1'bz;  // Controlled_Buffer controlled_buffer_5
  assign selMEM = and_4_out ? 1'b1 : 1'bz;  // Controlled_Buffer controlled_buffer_6
  assign strMEM = and_4_out ? 1'b0 : 1'bz;  // Controlled_Buffer controlled_buffer_7
  assign clrMEM = and_4_out ? 1'b0 : 1'bz;  // Controlled_Buffer controlled_buffer_8
  assign MuxASel = and_4_out ? 2'b01 : 2'bz;  // Controlled_Buffer controlled_buffer_9
  assign FunSel2a = and_4_out ? 2'b01 : 2'bz;  // Controlled_Buffer controlled_buffer_10
  assign RegSel2a = and_4_out ? decoder_2_out0 : 4'bz;  // Controlled_Buffer controlled_buffer_11
  hw2part2_main main_1 (
    .IR({IR_t, DESTREG, ADD__MOD, _1MSB, _1SEL, _2MSB, _2SEL, ADDRESS}), .ZCNO_Register({Z, C, N, O}),
    .MuxCSel(MuxCSel), .MuxASel(MuxASel), .OutBSel(OutBSel), .OutASel(OutASel), .FunSel2a(FunSel2a),
    .FunSel2c(FunSel2c), .RegSel2a(RegSel2a), .nL_H(nL_H), .E2c(Enable2c), .MuxBSel(MuxBSel),
    .OutDSel(OutDSel), .FunSelALU(FunSelALU), .OutCSel(OutCSel), .FunSel2b(FunSel2b), .RegSel2b(RegSel2b),
    .strMEM(strMEM), .selMEM(selMEM), .ldMEM(ldMEM), .clrMEM(clrMEM));
  assign RegSel2b = T0 ? 3'b001 : 3'bz;  // Controlled_Buffer controlled_buffer_12
  assign FunSel2b = T0 ? 2'b10 : 2'bz;  // Controlled_Buffer controlled_buffer_13
  assign OutDSel = T0 ? 2'b00 : 2'bz;  // Controlled_Buffer controlled_buffer_14
  assign ldMEM = T0 ? 1'b1 : 1'bz;  // Controlled_Buffer controlled_buffer_15
  assign selMEM = T0 ? 1'b1 : 1'bz;  // Controlled_Buffer controlled_buffer_16
  assign strMEM = T0 ? 1'b0 : 1'bz;  // Controlled_Buffer controlled_buffer_17
  assign clrMEM = T0 ? 1'b0 : 1'bz;  // Controlled_Buffer controlled_buffer_18
  assign nL_H = T0 ? 1'b1 : 1'bz;  // Controlled_Buffer controlled_buffer_19
  assign Enable2c = T0 ? 1'b1 : 1'bz;  // Controlled_Buffer controlled_buffer_20
  assign FunSel2c = T0 ? 2'b11 : 2'bz;  // Controlled_Buffer controlled_buffer_21
  and and_5 (Res1, D1, T4);
  and and_6 (and_6_out, D1, T3);
  assign OutASel = and_6_out ? DESTREG : 2'bz;  // Controlled_Buffer controlled_buffer_22
  assign MuxASel = and_6_out ? 2'b01 : 2'bz;  // Controlled_Buffer controlled_buffer_23
  assign MuxCSel = and_6_out ? 1'b1 : 1'bz;  // Controlled_Buffer controlled_buffer_24
  assign FunSelALU = and_6_out ? 4'b0000 : 4'bz;  // Controlled_Buffer controlled_buffer_25
  assign ldMEM = and_6_out ? 1'b0 : 1'bz;  // Controlled_Buffer controlled_buffer_26
  assign selMEM = and_6_out ? 1'b1 : 1'bz;  // Controlled_Buffer controlled_buffer_27
  assign strMEM = and_6_out ? 1'b1 : 1'bz;  // Controlled_Buffer controlled_buffer_28
  assign clrMEM = and_6_out ? 1'b0 : 1'bz;  // Controlled_Buffer controlled_buffer_29
  assign OutDSel = and_6_out ? 2'b01 : 2'bz;  // Controlled_Buffer controlled_buffer_30
  assign RegSel2b = T1 ? 3'b001 : 3'bz;  // Controlled_Buffer controlled_buffer_31
  assign FunSel2b = T1 ? 2'b10 : 2'bz;  // Controlled_Buffer controlled_buffer_32
  assign OutDSel = T1 ? 2'b00 : 2'bz;  // Controlled_Buffer controlled_buffer_33
  assign ldMEM = T1 ? 1'b1 : 1'bz;  // Controlled_Buffer controlled_buffer_34
  assign selMEM = T1 ? 1'b1 : 1'bz;  // Controlled_Buffer controlled_buffer_35
  assign strMEM = T1 ? 1'b0 : 1'bz;  // Controlled_Buffer controlled_buffer_36
  assign clrMEM = T1 ? 1'b0 : 1'bz;  // Controlled_Buffer controlled_buffer_37
  assign nL_H = T1 ? 1'b0 : 1'bz;  // Controlled_Buffer controlled_buffer_38
  assign Enable2c = T1 ? 1'b1 : 1'bz;  // Controlled_Buffer controlled_buffer_39
  assign FunSel2c = T1 ? 2'b11 : 2'bz;  // Controlled_Buffer controlled_buffer_40
  or or_1 (or_1_out, D2, Db, Dc, Dd);
  assign Enable2c = T2 ? 1'b0 : 1'bz;  // Controlled_Buffer controlled_buffer_41
  and and_7 (and_7_out, DESTREG[2], not_2_out);
  not not_2 (not_2_out, _1MSB);
  and and_8 (and_8_out, and_7_out, and_11_out);
  Multiplexer #(.select(2), .width(3), .enable("false")) multiplexer_1 (
    .in0(3'b001), .in1(3'b001), .in2(3'b010), .in3(3'b100), .out(multiplexer_1_out),
    .sel({DESTREG[1], ADD__MOD}));
  not not_3 (not_3_out, DESTREG[2]);
  and and_9 (and_9_out, not_3_out, _1MSB);
  and and_10 (and_10_out, and_9_out, and_11_out);
  Multiplexer #(.select(2), .width(4), .enable("false")) multiplexer_2 (
    .in0(4'b0001), .in1(4'b0010), .in2(4'b0100), .in3(4'b1000), .out(multiplexer_2_out),
    .sel({DESTREG[1], ADD__MOD}));
  and and_11 (and_11_out, or_1_out, T3);
  assign OutASel = and_8_out ? _1SEL : 2'bz;  // Controlled_Buffer controlled_buffer_42
  assign MuxBSel = and_8_out ? 2'b11 : 2'bz;  // Controlled_Buffer controlled_buffer_43
  assign FunSel2b = and_8_out ? 2'b01 : 2'bz;  // Controlled_Buffer controlled_buffer_44
  assign RegSel2b = and_8_out ? multiplexer_1_out : 3'bz;  // Controlled_Buffer controlled_buffer_45
  assign FunSelALU = and_8_out ? ALUFunSelCh : 4'bz;  // Controlled_Buffer controlled_buffer_46
  assign MuxCSel = and_8_out ? 1'b1 : 1'bz;  // Controlled_Buffer controlled_buffer_47
  assign OutCSel = and_10_out ? _1SEL : 2'bz;  // Controlled_Buffer controlled_buffer_48
  assign MuxASel = and_10_out ? 2'b10 : 2'bz;  // Controlled_Buffer controlled_buffer_49
  assign FunSel2a = and_10_out ? 2'b01 : 2'bz;  // Controlled_Buffer controlled_buffer_50
  assign RegSel2a = and_10_out ? multiplexer_2_out : 4'bz;  // Controlled_Buffer controlled_buffer_51
  assign FunSelALU = and_10_out ? ALUFunSelCh : 4'bz;  // Controlled_Buffer controlled_buffer_52
  or or_2 (or_2_out, D2, Db, Dc, Dd);
  Decoder #(.select(5), .enable("false")) decoder_3 (
    .out0(D0), .out1(D1), .out2(D2), .out3(D3), .out4(D4), .out5(D5), .out6(D6), .out7(D7), .out8(D8),
    .out9(D9), .out10(Da), .out11(Db), .out12(Dc), .out13(Dd), .out14(De), .out15(Df), .out16(Dg),
    .out17(Dh), .out18(Di), .sel(IR_t));  // open: out19, out20, out21, out22, out23, out24, out25, out26, out27, out28, out29, out30, out31
  and and_12 (ResALU1, or_2_out, T4);
  or or_3 (TYPE_2_INSTR, D2, D3, D4, D5, D6, D7, D8, D9, Da, Db, Dc, Dd, Di);
  Hex_Digit_Display hex_digit_display_1 (.value(IR_t[15:12]));  // open: dp
  Hex_Digit_Display hex_digit_display_2 (.value({IR_t[11], DESTREG, ADD__MOD}));  // open: dp
  Multiplexer #(.select(2), .width(2), .enable("false")) multiplexer_3 (
    .in0(2'b00), .in1(2'b00), .in2(2'b01), .in3(2'b10), .out(multiplexer_3_out), .sel(_1SEL));
  not not_4 (TYPE_1_INSTR, TYPE_2_INSTR);
  Hex_Digit_Display hex_digit_display_3 (.value({_1MSB, _1SEL, _2MSB}));  // open: dp
  Hex_Digit_Display hex_digit_display_4 (.value({_2SEL, ADDRESS}));  // open: dp
  not not_5 (not_5_out, DESTREG[2]);
  and and_13 (and_13_out, not_5_out, not_6_out);
  not not_6 (not_6_out, _1MSB);
  Multiplexer #(.select(2), .width(4), .enable("false")) multiplexer_4 (
    .in0(4'b0001), .in1(4'b0010), .in2(4'b0100), .in3(4'b1000), .out(multiplexer_4_out),
    .sel({DESTREG[1], ADD__MOD}));
  and and_14 (and_14_out, DESTREG[2], _1MSB);
  Multiplexer #(.select(2), .width(3), .enable("false")) multiplexer_5 (
    .in0(3'b001), .in2(3'b010), .in3(3'b100), .out(multiplexer_5_out), .sel({DESTREG[1], ADD__MOD}));  // open: in1
  and and_15 (and_15_out, and_13_out, and_11_out);
  assign MuxCSel = and_15_out ? 1'b1 : 1'bz;  // Controlled_Buffer controlled_buffer_53
  assign MuxASel = and_15_out ? 2'b11 : 2'bz;  // Controlled_Buffer controlled_buffer_54
  assign FunSel2a = and_15_out ? 2'b01 : 2'bz;  // Controlled_Buffer controlled_buffer_55
  assign RegSel2a = and_15_out ? multiplexer_4_out : 4'bz;  // Controlled_Buffer controlled_buffer_56
  assign OutASel = and_15_out ? _1SEL : 2'bz;  // Controlled_Buffer controlled_buffer_57
  assign FunSelALU = and_15_out ? ALUFunSelCh : 4'bz;  // Controlled_Buffer controlled_buffer_58
  and and_16 (and_16_out, and_14_out, and_11_out);
  assign MuxCSel = and_16_out ? 1'b0 : 1'bz;  // Controlled_Buffer controlled_buffer_59
  assign MuxASel = and_16_out ? 2'b10 : 2'bz;  // Controlled_Buffer controlled_buffer_60
  assign FunSel2b = and_16_out ? 2'b01 : 2'bz;  // Controlled_Buffer controlled_buffer_61
  assign RegSel2b = and_16_out ? multiplexer_5_out : 3'bz;  // Controlled_Buffer controlled_buffer_62
  assign OutCSel = and_16_out ? multiplexer_3_out : 2'bz;  // Controlled_Buffer controlled_buffer_63
  assign FunSelALU = and_16_out ? ALUFunSelCh : 4'bz;  // Controlled_Buffer controlled_buffer_64
  assign MuxBSel = and_16_out ? 2'b11 : 2'bz;  // Controlled_Buffer controlled_buffer_65
  or or_4 (or_4_out, Res0, Res1, Res3, Res4);
  not not_7 (not_7_out, DESTREG[2]);
  not not_8 (not_8_out, _1MSB);
  not not_9 (not_9_out, _2MSB);
  not not_10 (not_10_out, _1MSB);
  not not_11 (not_11_out, _2MSB);
  or or_5 (or_5_out, Res_efg, Resh, Resi);
  or or_6 (Reset, or_4_out, or_5_out, or_8_out);
  or or_7 (or_7_out, D5, D6, D9, Da);
  and and_17 (and_17_out, not_7_out, not_8_out, not_9_out);
  and and_18 (and_18_out, DESTREG[2], not_10_out, not_11_out);
  and and_19 (and_19_out, or_7_out, T3);
  and and_20 (and_20_out, and_17_out, and_19_out);
  assign OutASel = and_20_out ? _1SEL : 2'bz;  // Controlled_Buffer controlled_buffer_66
  assign OutBSel = and_20_out ? _2SEL : 2'bz;  // Controlled_Buffer controlled_buffer_67
  assign MuxCSel = and_20_out ? 1'b1 : 1'bz;  // Controlled_Buffer controlled_buffer_68
  assign FunSelALU = and_20_out ? ALUFunSelCh : 4'bz;  // Controlled_Buffer controlled_buffer_69
  assign MuxASel = and_20_out ? 2'b11 : 2'bz;  // Controlled_Buffer controlled_buffer_70
  assign FunSel2a = and_20_out ? 2'b01 : 2'bz;  // Controlled_Buffer controlled_buffer_71
  assign RegSel2a = and_20_out ? multiplexer_6_out : 4'bz;  // Controlled_Buffer controlled_buffer_72
  Multiplexer #(.select(2), .width(4), .enable("false")) multiplexer_6 (
    .in0(4'b0001), .in1(4'b0010), .in2(4'b0100), .in3(4'b1000), .out(multiplexer_6_out),
    .sel({DESTREG[1], ADD__MOD}));
  and and_21 (and_21_out, and_18_out, and_19_out);
  assign OutASel = and_21_out ? _1SEL : 2'bz;  // Controlled_Buffer controlled_buffer_73
  assign OutBSel = and_21_out ? _2SEL : 2'bz;  // Controlled_Buffer controlled_buffer_74
  assign MuxCSel = and_21_out ? 1'b1 : 1'bz;  // Controlled_Buffer controlled_buffer_75
  assign FunSelALU = and_21_out ? ALUFunSelCh : 4'bz;  // Controlled_Buffer controlled_buffer_76
  assign MuxASel = and_21_out ? 2'b11 : 2'bz;  // Controlled_Buffer controlled_buffer_77
  assign FunSel2a = and_21_out ? 2'b01 : 2'bz;  // Controlled_Buffer controlled_buffer_78
  Multiplexer #(.select(2), .width(3), .enable("false")) multiplexer_7 (
    .in0(3'b001), .in1(3'b001), .in2(3'b010), .in3(3'b100), .out(multiplexer_7_out),
    .sel({DESTREG[1], ADD__MOD}));
  assign RegSel2b = and_21_out ? multiplexer_7_out : 3'bz;  // Controlled_Buffer controlled_buffer_79
  or or_8 (or_8_out, ResALU1, ResetBonus, ResALU2, Res7_8);
  or or_9 (or_9_out, D5, D6, D9, Da);
  Multiplexer #(.select(4), .width(4), .enable("false")) multiplexer_8 (
    .in2(4'b0000), .in5(4'b0100), .in6(4'b0110), .in9(4'b0111), .in10(4'b1000), .in11(4'b0010),
    .in12(4'b1010), .in13(4'b1011), .out(ALUFunSelCh), .sel(IR_t[14:11]));  // open: in0, in1, in3, in4, in7, in8, in14, in15
  Multiplexer #(.select(2), .width(2), .enable("false")) multiplexer_9 (
    .in0(2'b00), .in1(2'b00), .in2(2'b01), .in3(2'b10), .out(multiplexer_9_out), .sel(_1SEL));
  and and_22 (ResALU2, or_9_out, not_15_out, T4);
  not not_12 (not_12_out, _2MSB);
  and and_23 (and_23_out, DESTREG[2], _1MSB, not_12_out);
  and and_24 (and_24_out, and_23_out, and_19_out);
  assign OutCSel = and_24_out ? multiplexer_9_out : 2'bz;  // Controlled_Buffer controlled_buffer_80
  assign OutBSel = and_24_out ? _2SEL : 2'bz;  // Controlled_Buffer controlled_buffer_81
  assign MuxASel = and_24_out ? 2'b10 : 2'bz;  // Controlled_Buffer controlled_buffer_82
  assign FunSelALU = and_24_out ? ALUFunSelCh : 4'bz;  // Controlled_Buffer controlled_buffer_83
  assign MuxCSel = and_24_out ? 1'b0 : 1'bz;  // Controlled_Buffer controlled_buffer_84
  assign MuxBSel = and_24_out ? 2'b11 : 2'bz;  // Controlled_Buffer controlled_buffer_85
  assign FunSel2b = and_24_out ? 2'b01 : 2'bz;  // Controlled_Buffer controlled_buffer_86
  Multiplexer #(.select(2), .width(3), .enable("false")) multiplexer_10 (
    .in0(3'b001), .in1(3'b001), .in2(3'b010), .in3(3'b100), .out(multiplexer_10_out),
    .sel({DESTREG[1], ADD__MOD}));
  assign RegSel2b = and_24_out ? multiplexer_10_out : 3'bz;  // Controlled_Buffer controlled_buffer_87
  not not_13 (not_13_out, DESTREG[2]);
  not not_14 (not_14_out, _2MSB);
  not not_15 (not_15_out, and_25_out);
  and and_25 (and_25_out, not_13_out, _1MSB, not_14_out);
  or or_10 (or_10_out, De, Df, Dg);
  and and_26 (and_26_out, De, T3);
  and and_27 (Res_efg, or_10_out, T5);
  and and_28 (and_28_out, Df, T3);
  and and_29 (and_29_out, and_28_out, Z);
  or or_11 (or_11_out, and_26_out, and_29_out, and_31_out);
  assign MuxBSel = or_11_out ? 2'b01 : 2'bz;  // Controlled_Buffer controlled_buffer_88
  assign RegSel2b = or_11_out ? 3'b001 : 3'bz;  // Controlled_Buffer controlled_buffer_89
  assign FunSel2b = or_11_out ? 2'b01 : 2'bz;  // Controlled_Buffer controlled_buffer_90
  and and_30 (and_30_out, Dg, T3);
  not not_16 (not_16_out, Z);
  and and_31 (and_31_out, not_16_out, and_30_out);
  and and_32 (and_32_out, Dh, T3);
  assign OutDSel = and_32_out ? 2'b10 : 2'bz;  // Controlled_Buffer controlled_buffer_91
  assign ldMEM = and_32_out ? 1'b0 : 1'bz;  // Controlled_Buffer controlled_buffer_92
  assign selMEM = and_32_out ? 1'b1 : 1'bz;  // Controlled_Buffer controlled_buffer_93
  assign strMEM = and_32_out ? 1'b1 : 1'bz;  // Controlled_Buffer controlled_buffer_94
  assign clrMEM = and_32_out ? 1'b0 : 1'bz;  // Controlled_Buffer controlled_buffer_95
  assign OutCSel = and_32_out ? 2'b00 : 2'bz;  // Controlled_Buffer controlled_buffer_96
  assign MuxASel = and_32_out ? 2'b10 : 2'bz;  // Controlled_Buffer controlled_buffer_97
  assign MuxCSel = and_32_out ? 1'b0 : 1'bz;  // Controlled_Buffer controlled_buffer_98
  assign FunSelALU = and_32_out ? 4'b0000 : 4'bz;  // Controlled_Buffer controlled_buffer_99
  assign FunSel2b = and_32_out ? 2'b11 : 2'bz;  // Controlled_Buffer controlled_buffer_100
  assign RegSel2b = and_32_out ? 3'b100 : 3'bz;  // Controlled_Buffer controlled_buffer_101
  and and_33 (and_33_out, Dh, T4);
  assign MuxBSel = and_33_out ? 2'b01 : 2'bz;  // Controlled_Buffer controlled_buffer_102
  assign RegSel2b = and_33_out ? 3'b001 : 3'bz;  // Controlled_Buffer controlled_buffer_103
  assign FunSel2b = and_33_out ? 2'b01 : 2'bz;  // Controlled_Buffer controlled_buffer_104
  assign FunSelALU = and_33_out ? 4'b0000 : 4'bz;  // Controlled_Buffer controlled_buffer_105
  assign OutCSel = and_33_out ? 2'b10 : 2'bz;  // Controlled_Buffer controlled_buffer_106
  assign MuxASel = and_33_out ? 2'b10 : 2'bz;  // Controlled_Buffer controlled_buffer_107
  assign MuxCSel = and_33_out ? 1'b0 : 1'bz;  // Controlled_Buffer controlled_buffer_108
  assign ldMEM = and_33_out ? 1'b0 : 1'bz;  // Controlled_Buffer controlled_buffer_109
  assign selMEM = and_33_out ? 1'b1 : 1'bz;  // Controlled_Buffer controlled_buffer_110
  assign strMEM = and_33_out ? 1'b0 : 1'bz;  // Controlled_Buffer controlled_buffer_111
  assign clrMEM = and_33_out ? 1'b0 : 1'bz;  // Controlled_Buffer controlled_buffer_112
  and and_34 (Resh, Dh, T5);
  and and_35 (and_35_out, Di, T3);
  assign FunSel2b = and_35_out ? 2'b10 : 2'bz;  // Controlled_Buffer controlled_buffer_113
  assign RegSel2b = and_35_out ? 3'b100 : 3'bz;  // Controlled_Buffer controlled_buffer_114
  and and_36 (and_36_out, Di, T5);
  assign FunSelALU = and_36_out ? 4'b0000 : 4'bz;  // Controlled_Buffer controlled_buffer_115
  assign OutCSel = and_36_out ? 2'b10 : 2'bz;  // Controlled_Buffer controlled_buffer_116
  assign MuxASel = and_36_out ? 2'b10 : 2'bz;  // Controlled_Buffer controlled_buffer_117
  assign MuxCSel = and_36_out ? 1'b0 : 1'bz;  // Controlled_Buffer controlled_buffer_118
  assign ldMEM = and_36_out ? 1'b0 : 1'bz;  // Controlled_Buffer controlled_buffer_119
  assign selMEM = and_36_out ? 1'b1 : 1'bz;  // Controlled_Buffer controlled_buffer_120
  assign strMEM = and_36_out ? 1'b0 : 1'bz;  // Controlled_Buffer controlled_buffer_121
  assign clrMEM = and_36_out ? 1'b0 : 1'bz;  // Controlled_Buffer controlled_buffer_122
  and and_37 (and_37_out, Di, T4);
  assign MuxBSel = and_37_out ? 2'b10 : 2'bz;  // Controlled_Buffer controlled_buffer_123
  assign RegSel2b = and_37_out ? 3'b001 : 3'bz;  // Controlled_Buffer controlled_buffer_124
  assign FunSel2b = and_37_out ? 2'b01 : 2'bz;  // Controlled_Buffer controlled_buffer_125
  assign OutDSel = and_37_out ? 2'b10 : 2'bz;  // Controlled_Buffer controlled_buffer_126
  assign ldMEM = and_37_out ? 1'b1 : 1'bz;  // Controlled_Buffer controlled_buffer_127
  assign selMEM = and_37_out ? 1'b1 : 1'bz;  // Controlled_Buffer controlled_buffer_128
  assign strMEM = and_37_out ? 1'b0 : 1'bz;  // Controlled_Buffer controlled_buffer_129
  assign clrMEM = and_37_out ? 1'b0 : 1'bz;  // Controlled_Buffer controlled_buffer_130
  and and_38 (Resi, Di, T6);
  and and_39 (and_39_out, D3, T3);
  assign OutDSel = and_39_out ? 2'b10 : 2'bz;  // Controlled_Buffer controlled_buffer_131
  assign ldMEM = and_39_out ? 1'b0 : 1'bz;  // Controlled_Buffer controlled_buffer_132
  assign selMEM = and_39_out ? 1'b1 : 1'bz;  // Controlled_Buffer controlled_buffer_133
  assign strMEM = and_39_out ? 1'b1 : 1'bz;  // Controlled_Buffer controlled_buffer_134
  assign clrMEM = and_39_out ? 1'b0 : 1'bz;  // Controlled_Buffer controlled_buffer_135
  assign MuxCSel = and_39_out ? 1'b1 : 1'bz;  // Controlled_Buffer controlled_buffer_136
  assign FunSelALU = and_39_out ? 4'b0000 : 4'bz;  // Controlled_Buffer controlled_buffer_137
  assign OutASel = and_39_out ? _1SEL : 2'bz;  // Controlled_Buffer controlled_buffer_138
  assign FunSel2b = and_39_out ? 2'b11 : 2'bz;  // Controlled_Buffer controlled_buffer_139
  assign RegSel2b = and_39_out ? 3'b100 : 3'bz;  // Controlled_Buffer controlled_buffer_140
  and and_40 (and_40_out, D3, T4);
  assign FunSelALU = and_40_out ? 4'b0000 : 4'bz;  // Controlled_Buffer controlled_buffer_141
  assign OutCSel = and_40_out ? 2'b10 : 2'bz;  // Controlled_Buffer controlled_buffer_142
  assign MuxASel = and_40_out ? 2'b10 : 2'bz;  // Controlled_Buffer controlled_buffer_143
  assign MuxCSel = and_40_out ? 1'b0 : 1'bz;  // Controlled_Buffer controlled_buffer_144
  assign ldMEM = and_40_out ? 1'b0 : 1'bz;  // Controlled_Buffer controlled_buffer_145
  assign selMEM = and_40_out ? 1'b1 : 1'bz;  // Controlled_Buffer controlled_buffer_146
  assign strMEM = and_40_out ? 1'b0 : 1'bz;  // Controlled_Buffer controlled_buffer_147
  assign clrMEM = and_40_out ? 1'b0 : 1'bz;  // Controlled_Buffer controlled_buffer_148
  and and_41 (Res3, D3, T5);
  and and_42 (and_42_out, D4, T3);
  assign FunSel2b = and_42_out ? 2'b10 : 2'bz;  // Controlled_Buffer controlled_buffer_149
  assign RegSel2b = and_42_out ? 3'b100 : 3'bz;  // Controlled_Buffer controlled_buffer_150
  and and_43 (and_43_out, D4, T5);
  assign FunSelALU = and_43_out ? 4'b0000 : 4'bz;  // Controlled_Buffer controlled_buffer_151
  assign OutCSel = and_43_out ? 2'b10 : 2'bz;  // Controlled_Buffer controlled_buffer_152
  assign MuxASel = and_43_out ? 2'b10 : 2'bz;  // Controlled_Buffer controlled_buffer_153
  assign MuxCSel = and_43_out ? 1'b0 : 1'bz;  // Controlled_Buffer controlled_buffer_154
  assign ldMEM = and_43_out ? 1'b0 : 1'bz;  // Controlled_Buffer controlled_buffer_155
  assign selMEM = and_43_out ? 1'b1 : 1'bz;  // Controlled_Buffer controlled_buffer_156
  assign strMEM = and_43_out ? 1'b0 : 1'bz;  // Controlled_Buffer controlled_buffer_157
  assign clrMEM = and_43_out ? 1'b0 : 1'bz;  // Controlled_Buffer controlled_buffer_158
  and and_44 (Res4, D4, T6);
  and and_45 (and_45_out, D4, T4);
  assign OutDSel = and_45_out ? 2'b10 : 2'bz;  // Controlled_Buffer controlled_buffer_159
  Multiplexer #(.select(2), .width(4), .enable("false")) multiplexer_11 (
    .in0(4'b0001), .in1(4'b0010), .in2(4'b0100), .in3(4'b1000), .out(multiplexer_11_out),
    .sel({DESTREG[1], ADD__MOD}));
  assign RegSel2a = and_45_out ? multiplexer_11_out : 4'bz;  // Controlled_Buffer controlled_buffer_160
  assign FunSel2a = and_45_out ? 2'b01 : 2'bz;  // Controlled_Buffer controlled_buffer_161
  assign MuxASel = and_45_out ? 2'b01 : 2'bz;  // Controlled_Buffer controlled_buffer_162
  assign ldMEM = and_45_out ? 1'b1 : 1'bz;  // Controlled_Buffer controlled_buffer_163
  assign selMEM = and_45_out ? 1'b1 : 1'bz;  // Controlled_Buffer controlled_buffer_164
  assign strMEM = and_45_out ? 1'b0 : 1'bz;  // Controlled_Buffer controlled_buffer_165
  assign clrMEM = and_45_out ? 1'b0 : 1'bz;  // Controlled_Buffer controlled_buffer_166
  assign OutASel = and_45_out ? {DESTREG[1], ADD__MOD} : 2'bz;  // Controlled_Buffer controlled_buffer_167
  or or_12 (or_12_out, D7, D8);
  Multiplexer #(.select(2), .width(4), .enable("false")) multiplexer_12 (
    .in0(4'b0001), .in1(4'b0010), .in2(4'b0100), .in3(4'b1000), .out(multiplexer_12_out),
    .sel({DESTREG[1], ADD__MOD}));
  or or_13 (or_13_out, D7, D8);
  or or_14 (or_14_out, D7, D8);
  and and_46 (and_46_out, DESTREG[2], not_17_out);
  not not_17 (not_17_out, _1MSB);
  Multiplexer #(.select(2), .width(3), .enable("false")) multiplexer_13 (
    .in0(3'b001), .in1(3'b001), .in2(3'b010), .in3(3'b100), .out(multiplexer_13_out),
    .sel({DESTREG[1], ADD__MOD}));
  not not_18 (not_18_out, DESTREG[2]);
  and and_47 (and_47_out, not_18_out, _1MSB);
  Multiplexer #(.select(2), .width(4), .enable("false")) multiplexer_14 (
    .in0(4'b0001), .in1(4'b0010), .in2(4'b0100), .in3(4'b1000), .out(multiplexer_14_out),
    .sel({DESTREG[1], ADD__MOD}));
  and and_48 (and_48_out, or_12_out, D_S);
  and and_49 (and_49_out, and_48_out, T3);
  not not_19 (not_19_out, DESTREG[2]);
  Multiplexer #(.width(2), .enable("false")) multiplexer_15 (
    .in0(2'b11), .in1(2'b10), .out(multiplexer_15_out), .sel(D8));
  Multiplexer #(.width(2), .enable("false")) multiplexer_16 (
    .in0(2'b11), .in1(2'b10), .out(multiplexer_16_out), .sel(D8));
  Multiplexer #(.select(2), .width(3), .enable("false")) multiplexer_17 (
    .in0(3'b001), .in1(3'b001), .in2(3'b010), .in3(3'b100), .out(multiplexer_17_out),
    .sel({DESTREG[1], ADD__MOD}));
  and and_50 (and_50_out, or_13_out, D_S);
  and and_51 (and_51_out, and_50_out, T5);
  not not_20 (not_20_out, D_S);
  and and_52 (and_52_out, or_14_out, not_20_out);
  and and_53 (and_53_out, and_52_out, T3);
  and and_54 (and_54_out, and_46_out, and_53_out);
  assign OutASel = and_54_out ? _1SEL : 2'bz;  // Controlled_Buffer controlled_buffer_168
  assign MuxBSel = and_54_out ? 2'b11 : 2'bz;  // Controlled_Buffer controlled_buffer_169
  assign FunSel2b = and_54_out ? 2'b01 : 2'bz;  // Controlled_Buffer controlled_buffer_170
  assign RegSel2b = and_54_out ? multiplexer_13_out : 3'bz;  // Controlled_Buffer controlled_buffer_171
  assign FunSelALU = and_54_out ? 4'b0000 : 4'bz;  // Controlled_Buffer controlled_buffer_172
  assign MuxCSel = and_54_out ? 1'b1 : 1'bz;  // Controlled_Buffer controlled_buffer_173
  and and_55 (and_55_out, and_47_out, and_53_out);
  assign OutCSel = and_55_out ? _1SEL : 2'bz;  // Controlled_Buffer controlled_buffer_174
  assign MuxASel = and_55_out ? 2'b10 : 2'bz;  // Controlled_Buffer controlled_buffer_175
  assign FunSel2a = and_55_out ? 2'b01 : 2'bz;  // Controlled_Buffer controlled_buffer_176
  assign RegSel2a = and_55_out ? multiplexer_14_out : 4'bz;  // Controlled_Buffer controlled_buffer_177
  assign FunSelALU = and_55_out ? 4'b0000 : 4'bz;  // Controlled_Buffer controlled_buffer_178
  or or_15 (or_15_out, D7, D8);
  or or_16 (or_16_out, and_49_out, and_59_out);
  and and_56 (and_56_out, not_19_out, or_16_out);
  assign FunSel2a = and_56_out ? multiplexer_15_out : 2'bz;  // Controlled_Buffer controlled_buffer_179
  assign RegSel2a = and_56_out ? multiplexer_12_out : 4'bz;  // Controlled_Buffer controlled_buffer_180
  and and_57 (and_57_out, DESTREG[2], or_16_out);
  assign FunSel2b = and_57_out ? multiplexer_16_out : 2'bz;  // Controlled_Buffer controlled_buffer_181
  assign RegSel2b = and_57_out ? multiplexer_17_out : 3'bz;  // Controlled_Buffer controlled_buffer_182
  or or_17 (or_17_out, D7, D8);
  or or_18 (Res7_8, and_51_out, and_61_out);
  not not_21 (not_21_out, D_S);
  and and_58 (and_58_out, or_15_out, not_21_out);
  and and_59 (and_59_out, and_58_out, T4);
  not not_22 (not_22_out, D_S);
  and and_60 (and_60_out, or_17_out, not_22_out);
  and and_61 (and_61_out, and_60_out, T6);
  Multiplexer #(.select(2), .width(2), .enable("false")) multiplexer_18 (
    .in0(2'b00), .in1(2'b00), .in2(2'b01), .in3(2'b10), .out(multiplexer_18_out), .sel(_1SEL));
  not not_23 (not_23_out, DESTREG[2]);
  not not_24 (not_24_out, _1MSB);
  Multiplexer #(.select(2), .width(4), .enable("false")) multiplexer_19 (
    .in0(4'b0001), .in1(4'b0010), .in2(4'b0100), .in3(4'b1000), .out(multiplexer_19_out),
    .sel({DESTREG[1], ADD__MOD}));
  and and_62 (and_62_out, DESTREG[2], _1MSB);
  Multiplexer #(.select(2), .width(3), .enable("false")) multiplexer_20 (
    .in0(3'b001), .in1(3'b001), .in2(3'b010), .in3(3'b100), .out(multiplexer_20_out),
    .sel({DESTREG[1], ADD__MOD}));
  or or_19 (or_19_out, D7, D8);
  assign xor_1_out = {DESTREG, ADD__MOD} ^ {_1MSB, _1SEL};  // XOR_Gate xor_1, 3 bits wide
  and and_63 (and_63_out, not_23_out, not_24_out);
  and and_64 (and_64_out, and_63_out, and_53_out);
  assign MuxCSel = and_64_out ? 1'b1 : 1'bz;  // Controlled_Buffer controlled_buffer_183
  assign MuxASel = and_64_out ? 2'b11 : 2'bz;  // Controlled_Buffer controlled_buffer_184
  assign FunSel2a = and_64_out ? 2'b01 : 2'bz;  // Controlled_Buffer controlled_buffer_185
  assign RegSel2a = and_64_out ? multiplexer_19_out : 4'bz;  // Controlled_Buffer controlled_buffer_186
  assign OutASel = and_64_out ? _1SEL : 2'bz;  // Controlled_Buffer controlled_buffer_187
  assign FunSelALU = and_64_out ? 4'b0000 : 4'bz;  // Controlled_Buffer controlled_buffer_188
  and and_65 (and_65_out, and_62_out, and_53_out);
  assign MuxCSel = and_65_out ? 1'b0 : 1'bz;  // Controlled_Buffer controlled_buffer_189
  assign MuxASel = and_65_out ? 2'b10 : 2'bz;  // Controlled_Buffer controlled_buffer_190
  assign FunSel2b = and_65_out ? 2'b01 : 2'bz;  // Controlled_Buffer controlled_buffer_191
  assign RegSel2b = and_65_out ? multiplexer_20_out : 3'bz;  // Controlled_Buffer controlled_buffer_192
  assign OutCSel = and_65_out ? multiplexer_18_out : 2'bz;  // Controlled_Buffer controlled_buffer_193
  assign FunSelALU = and_65_out ? 4'b0000 : 4'bz;  // Controlled_Buffer controlled_buffer_194
  assign MuxBSel = and_65_out ? 2'b11 : 2'bz;  // Controlled_Buffer controlled_buffer_195
  and and_66 (and_66_out, or_19_out, D_S);
  and and_67 (and_67_out, and_66_out, T4);
  not not_25 (not_25_out, DESTREG[2]);
  and and_68 (and_68_out, not_25_out, or_22_out);
  and and_69 (and_69_out, DESTREG[2], or_22_out);
  assign FunSelALU = and_69_out ? 4'b0000 : 4'bz;  // Controlled_Buffer controlled_buffer_196
  assign OutCSel = and_69_out ? multiplexer_21_out : 2'bz;  // Controlled_Buffer controlled_buffer_197
  Multiplexer #(.select(2), .width(2), .enable("false")) multiplexer_21 (
    .in0(2'b00), .in1(2'b00), .in2(2'b01), .in3(2'b10), .out(multiplexer_21_out), .sel(_1SEL));
  assign MuxASel = and_69_out ? 2'b10 : 2'bz;  // Controlled_Buffer controlled_buffer_198
  assign MuxCSel = and_69_out ? 1'b0 : 1'bz;  // Controlled_Buffer controlled_buffer_199
  assign ldMEM = and_69_out ? 1'b0 : 1'bz;  // Controlled_Buffer controlled_buffer_200
  assign selMEM = and_69_out ? 1'b1 : 1'bz;  // Controlled_Buffer controlled_buffer_201
  assign strMEM = and_69_out ? 1'b0 : 1'bz;  // Controlled_Buffer controlled_buffer_202
  assign clrMEM = and_69_out ? 1'b0 : 1'bz;  // Controlled_Buffer controlled_buffer_203
  not not_26 (D_S, or_20_out);
  or or_20 (or_20_out, xor_1_out[0], xor_1_out[1], xor_1_out[2]);
  or or_21 (or_21_out, D7, D8);
  or or_22 (or_22_out, and_67_out, and_71_out);
  assign FunSelALU = and_68_out ? 4'b0000 : 4'bz;  // Controlled_Buffer controlled_buffer_204
  assign MuxCSel = and_68_out ? 1'b1 : 1'bz;  // Controlled_Buffer controlled_buffer_205
  assign OutASel = and_68_out ? {DESTREG[1], ADD__MOD} : 2'bz;  // Controlled_Buffer controlled_buffer_206
  assign ldMEM = and_68_out ? 1'b0 : 1'bz;  // Controlled_Buffer controlled_buffer_207
  assign selMEM = and_68_out ? 1'b1 : 1'bz;  // Controlled_Buffer controlled_buffer_208
  assign strMEM = and_68_out ? 1'b0 : 1'bz;  // Controlled_Buffer controlled_buffer_209
  assign clrMEM = and_68_out ? 1'b0 : 1'bz;  // Controlled_Buffer controlled_buffer_210
  not not_27 (not_27_out, D_S);
  and and_70 (and_70_out, or_21_out, not_27_out);
  and and_71 (and_71_out, and_70_out, T5);
  not not_28 (not_28_out, DESTREG[2]);
  not not_29 (not_29_out, _2MSB);
  or or_23 (or_23_out, D5, D6, D9, Da);
  and and_72 (and_72_out, not_28_out, _1MSB, not_29_out);
  Multiplexer #(.select(2), .width(2), .enable("false")) multiplexer_22 (
    .in0(2'b00), .in1(2'b00), .in2(2'b01), .in3(2'b10), .out(multiplexer_22_out), .sel(_1SEL));
  and and_73 (and_73_out, or_23_out, T3);
  and and_74 (and_74_out, and_72_out, and_73_out);
  assign OutCSel = and_74_out ? multiplexer_22_out : 2'bz;  // Controlled_Buffer controlled_buffer_211
  assign OutBSel = and_74_out ? _2SEL : 2'bz;  // Controlled_Buffer controlled_buffer_212
  assign MuxASel = and_74_out ? 2'b10 : 2'bz;  // Controlled_Buffer controlled_buffer_213
  assign FunSelALU = and_74_out ? ALUFunSelCh : 4'bz;  // Controlled_Buffer controlled_buffer_214
  assign MuxCSel = and_74_out ? 1'b0 : 1'bz;  // Controlled_Buffer controlled_buffer_215
  assign OutDSel = and_74_out ? 2'b10 : 2'bz;  // Controlled_Buffer controlled_buffer_216
  assign ldMEM = and_74_out ? 1'b0 : 1'bz;  // Controlled_Buffer controlled_buffer_217
  assign selMEM = and_74_out ? 1'b1 : 1'bz;  // Controlled_Buffer controlled_buffer_218
  assign strMEM = and_74_out ? 1'b1 : 1'bz;  // Controlled_Buffer controlled_buffer_219
  assign clrMEM = and_74_out ? 1'b0 : 1'bz;  // Controlled_Buffer controlled_buffer_220
  not not_30 (not_30_out, DESTREG[2]);
  not not_31 (not_31_out, _2MSB);
  or or_24 (or_24_out, D5, D6, D9, Da);
  and and_75 (and_75_out, not_30_out, _1MSB, not_31_out);
  and and_76 (and_76_out, or_24_out, T4);
  and and_77 (and_77_out, and_75_out, and_76_out);
  assign OutDSel = and_77_out ? 2'b10 : 2'bz;  // Controlled_Buffer controlled_buffer_221
  Multiplexer #(.select(2), .width(4), .enable("false")) multiplexer_23 (
    .in0(4'b0001), .in1(4'b0010), .in2(4'b0100), .in3(4'b1000), .out(multiplexer_23_out),
    .sel({DESTREG[1], ADD__MOD}));
  assign RegSel2a = and_77_out ? multiplexer_23_out : 4'bz;  // Controlled_Buffer controlled_buffer_222
  assign FunSel2a = and_77_out ? 2'b01 : 2'bz;  // Controlled_Buffer controlled_buffer_223
  assign MuxASel = and_77_out ? 2'b01 : 2'bz;  // Controlled_Buffer controlled_buffer_224
  assign ldMEM = and_77_out ? 1'b1 : 1'bz;  // Controlled_Buffer controlled_buffer_225
  assign selMEM = and_77_out ? 1'b1 : 1'bz;  // Controlled_Buffer controlled_buffer_226
  assign strMEM = and_77_out ? 1'b0 : 1'bz;  // Controlled_Buffer controlled_buffer_227
  assign clrMEM = and_77_out ? 1'b0 : 1'bz;  // Controlled_Buffer controlled_buffer_228
  assign OutASel = and_77_out ? {DESTREG[1], ADD__MOD} : 2'bz;  // Controlled_Buffer controlled_buffer_229
  or or_25 (or_25_out, D5, D6, D9, Da);
  not not_32 (not_32_out, DESTREG[2]);
  not not_33 (not_33_out, _2MSB);
  and and_78 (and_78_out, not_32_out, _1MSB, not_33_out);
  and and_79 (ResetBonus, and_78_out, and_80_out);
  and and_80 (and_80_out, or_25_out, T5);

  // Other names for the same wires on the sheet: IR_t[10:0] = {DESTREG, ADD__MOD, _1MSB, _1SEL, _2MSB, _2SEL, ADDRESS};
  //   ADDRESS[7:2] = {_1MSB, _1SEL, _2MSB, _2SEL}; SRCREG2[2:0] = {_2MSB, _2SEL}; SRCREG1[2:0] = {_1MSB, _1SEL};
  //   DESTREG[0] = ADD__MOD; DSEL[1:0] = {DESTREG[1], ADD__MOD}; REGSEL[1:0] = DESTREG; DMSB = DESTREG[2];
  //   OPCODE[4:0] = IR_t; ZCNO[3:0] = {Z, C, N, O}

  // Notes on the sheet:
  //   OPERATION FINISH ->
  //   ENCODER ->
  //   ENCODER ->
  //   0x00 - LD
  //   OPERATION FINISH ->
  //   IR(8-15) <- M[PC]
  //   PC <- PC + 1
  //   0x01 - ST
  //   FETCH DECODE CYCLE (T0-T2)
  //   IR(0-7) <- M[PC]
  //   PC <- PC + 1
  //   0x02 - MOV
  //   0x0B - NOT
  //   0x0C - LSL
  //   0x0D - LSR
  //   2b <- 2a
  //   2a <- 2b
  //   OPERATION FINISH ->
  //   CURRENT INSTRUCTION
  //   2a <- 2a
  //   2b <- 2b
  //   a <- a + a
  //   b <- a + a
  //   0x05 - ADD
  //   0x06 - SUB
  //   0x09 - AND
  //   0x0A - OR
  //   b <- b + a
  //   ALU Decoder
  //   0x0E - BRA
  //   0x0F - BEQ
  //   0x10 - BNE
  //   PC <- Value
  //   CORG GROUP 31
  //   0x11 - CALL
  //   M[SP] <- PC
  //   SP <- SP - 1
  //   PC <- Value
  //   ALU Flag Update
  //   0x12 - RET
  //   ALU Flag Update
  //   SP <- SP + 1
  //   PC <- M[SP]
  //   0x03 - PSH
  //   M[SP] <- Rx
  //   SP <- SP - 1
  //   ALU Flag Update
  //   0x04 - PUL
  //   SP <- SP + 1
  //   ALU Flag Update
  //   Rx <- M[SP]
  //   OPERATION FINISH ->
  //   0x08 - INC
  //   0x07 - DEC
  //   2b <- 2a
  //   2a <- 2b
  //   2b <- 2a
  //   2a <- 2a
  //   2a <- 2b
  //   ALU Flag Update
  //   ALU Flag Update
  //   2a <- 2a
  //   2b <- 2b
  //   a <- b + a
  //   0x05 - ADD
  //   0x06 - SUB
  //   0x09 - AND
  //   0x0A - OR
  //   M[SP] <- ALU
  //   ALU <- M[SP]
endmodule

module seq_counter (
  input  RESET,
  output T7,
  output T6,
  output T5,
  output T4,
  output T3,
  output T2,
  output T1,
  output T0
);

  wire clock_1_out;
  wire [1:0] multiplexer_1_out;
  wire [3:0] main_1_output;

  Clock clock_1 (.out(clock_1_out));
  part1_8_main main_1 (
    .CLK(clock_1_out), .OUTPUT(main_1_output), .SELECTION(multiplexer_1_out), .ENABLE(1'b1));  // open: INPUT
  Decoder #(.select(3), .enable("false")) decoder_1 (
    .out0(T0), .out1(T1), .out2(T2), .out3(T3), .out4(T4), .out5(T5), .out6(T6), .out7(T7),
    .sel(main_1_output[2:0]));
  Multiplexer #(.width(2), .enable("false")) multiplexer_1 (
    .in0(2'b10), .in1(2'b00), .out(multiplexer_1_out), .sel(RESET));
endmodule
