// Logisim project part1_8.circ as structural Verilog: 2 circuits, main circuit main
module main (
  input  CLK,
  input  [1:0] SELECTION,
  input  ENABLE,
  input  [3:0] INPUT,
  output [3:0] OUTPUT
);

  wire and_1_out, and_2_out, or_1_out, or_2_out;

  or or_1 (or_1_out, OUTPUT[2], or_2_out);
  and and_1 (and_1_out, OUTPUT[2], and_2_out);
  _1_bit_op u_1_bit_op_1 (
    .CLK(CLK), .CLEAR(1'b0), .INPUT(INPUT[3]), .INCREMENT(and_1_out), .DECREMENT(or_1_out),
    .SELECTION(SELECTION), .ENABLE(ENABLE), .OUTPUT(OUTPUT[3]));
  or or_2 (or_2_out, OUTPUT[1], OUTPUT[0]);
  and and_2 (and_2_out, OUTPUT[1], OUTPUT[0]);
  _1_bit_op u_1_bit_op_2 (
    .CLK(CLK), .CLEAR(1'b0), .INPUT(INPUT[2]), .INCREMENT(and_2_out), .DECREMENT(or_2_out),
    .SELECTION(SELECTION), .ENABLE(ENABLE), .OUTPUT(OUTPUT[2]));
  _1_bit_op u_1_bit_op_3 (
    .CLK(CLK), .CLEAR(1'b0), .INPUT(INPUT[1]), .INCREMENT(OUTPUT[0]), .DECREMENT(OUTPUT[0]),
    .SELECTION(SELECTION), .ENABLE(ENABLE), .OUTPUT(OUTPUT[1]));
  _1_bit_op u_1_bit_op_4 (
    .CLK(CLK), .CLEAR(1'b0), .INPUT(INPUT[0]), .INCREMENT(1'b1), .DECREMENT(1'b0), .SELECTION(SELECTION),
    .ENABLE(ENABLE), .OUTPUT(OUTPUT[0]));
endmodule

module _1_bit_op (
  input  CLK,
  input  CLEAR,
  input  INPUT,
  input  [1:0] SELECTION,
  input  ENABLE,
  input  DECREMENT,
  input  INCREMENT,
  output OUTPUT
);

  wire multiplexer_1_out, xnor_1_out, xor_1_out;

  xor xor_1 (xor_1_out, INCREMENT, OUTPUT);
  xnor xnor_1 (xnor_1_out, DECREMENT, OUTPUT);
  Multiplexer #(.select(2), .enable("false")) multiplexer_1 (
    .in0(CLEAR), .in1(INPUT), .in2(xor_1_out), .in3(xnor_1_out), .out(multiplexer_1_out), .sel(SELECTION));
  D_Flip_Flop d_ff_1 (.clk(CLK), .D(multiplexer_1_out), .Q(OUTPUT), .en(ENABLE));  // open: Qn, preset, reset

  // Notes on the sheet:
  //   Bit n XNOR (Bit n-1 OR (Bit n-2 OR (... OR Bit 0)))
  //   Bit n XOR (Bit n-1 AND (Bit n-2 AND (... AND Bit 0)))
endmodule
