// Logisim project part2c.circ as structural Verilog: 3 circuits, main circuit main
module main (
  input  EN,
  input  [1:0] FunSel,
  input  [7:0] in_3,
  input  nL_H,
  output [15:0] out_5
);

  wire clock_1_out;
  wire [1:0] multiplexer_2_out;
  wire [15:0] multiplexer_1_out;

  Clock clock_1 (.out(clock_1_out));
  _16_bit_circuit u_16_bit_circuit_1 (
    .STATIC_0(1'b0), .STATIC_1(1'b1), .CLK(clock_1_out), .OUTPUT(out_5), .INPUT(multiplexer_1_out),
    .SELECTION(multiplexer_2_out), .ENABLE(EN));
  Multiplexer #(.width(16), .enable("false")) multiplexer_1 (
    .in0({out_5[15:8], in_3}), .in1({in_3, out_5[7:0]}), .out(multiplexer_1_out), .sel(nL_H));
  Hex_Digit_Display hex_digit_display_1 (.value(out_5[15:12]));  // open: dp
  Hex_Digit_Display hex_digit_display_2 (.value(out_5[11:8]));  // open: dp
  Hex_Digit_Display hex_digit_display_3 (.value(out_5[3:0]));  // open: dp
  Hex_Digit_Display hex_digit_display_4 (.value(out_5[7:4]));  // open: dp
  Multiplexer #(.select(2), .width(2), .enable("false")) multiplexer_2 (
    .in0(2'b00), .in1(2'b10), .in2(2'b11), .in3(2'b01), .out(multiplexer_2_out), .sel(FunSel));
  Hex_Digit_Display hex_digit_display_5 (.value(in_3[7:4]));  // open: dp
  Hex_Digit_Display hex_digit_display_6 (.value(in_3[3:0]));  // open: dp
endmodule

module _1_bit_op (
  input  CLK,
  input  CLEAR,
  input  INPUT,
  input  [1:0] SELECTION,
  input  ENABLE,
  input  DECREMENT,
  input  INCREMENT,
  output OUTPUT
);

  wire multiplexer_1_out, xnor_1_out, xor_1_out;

  xor xor_1 (xor_1_out, INCREMENT, OUTPUT);
  xnor xnor_1 (xnor_1_out, DECREMENT, OUTPUT);
  Multiplexer #(.select(2), .enable("false")) multiplexer_1 (
    .in0(CLEAR), .in1(INPUT), .in2(xor_1_out), .in3(xnor_1_out), .out(multiplexer_1_out), .sel(SELECTION));
  D_Flip_Flop d_ff_1 (.clk(CLK), .D(multiplexer_1_out), .Q(OUTPUT), .en(ENABLE));  // open: Qn, preset, reset

  // Notes on the sheet:
  //   Bit n XNOR (Bit n-1 OR (Bit n-2 OR (... OR Bit 0)))
  //   Bit n XOR (Bit n-1 AND (Bit n-2 AND (... AND Bit 0)))
endmodule

module _16_bit_circuit (
  input  CLK,
  input  [1:0] SELECTION,
  input  ENABLE,
  input  STATIC_0,
  input  STATIC_1,
  input  [15:0] INPUT,
  output [15:0] OUTPUT
);

  wire and_1_out, and_2_out, and_3_out, and_4_out, and_5_out, and_6_out, and_7_out, and_8_out, and_9_out,
       and_10_out, and_11_out, and_12_out, and_13_out, and_14_out, or_1_out, or_2_out, or_3_out, or_4_out,
       or_5_out, or_6_out, or_7_out, or_8_out, or_9_out, or_10_out, or_11_out, or_12_out, or_13_out,
       or_14_out;

  Clock clock_1 ();  // open: out
  _1_bit_op u_1_bit_op_1 (
    .CLK(CLK), .CLEAR(STATIC_0), .INPUT(INPUT[15]), .INCREMENT(and_1_out), .DECREMENT(or_1_out),
    .SELECTION(SELECTION), .ENABLE(ENABLE), .OUTPUT(OUTPUT[15]));
  or or_1 (or_1_out, OUTPUT[14], or_2_out);
  and and_1 (and_1_out, OUTPUT[14], and_2_out);
  _1_bit_op u_1_bit_op_2 (
    .CLK(CLK), .CLEAR(STATIC_0), .INPUT(INPUT[14]), .INCREMENT(and_2_out), .DECREMENT(or_2_out),
    .SELECTION(SELECTION), .ENABLE(ENABLE), .OUTPUT(OUTPUT[14]));
  or or_2 (or_2_out, OUTPUT[13], or_3_out);
  and and_2 (and_2_out, OUTPUT[13], and_3_out);
  or or_3 (or_3_out, OUTPUT[12], or_4_out);
  and and_3 (and_3_out, OUTPUT[12], and_4_out);
  _1_bit_op u_1_bit_op_3 (
    .CLK(CLK), .CLEAR(STATIC_0), .INPUT(INPUT[13]), .INCREMENT(and_3_out), .DECREMENT(or_3_out),
    .SELECTION(SELECTION), .ENABLE(ENABLE), .OUTPUT(OUTPUT[13]));
  or or_4 (or_4_out, OUTPUT[11], or_5_out);
  and and_4 (and_4_out, OUTPUT[11], and_5_out);
  _1_bit_op u_1_bit_op_4 (
    .CLK(CLK), .CLEAR(STATIC_0), .INPUT(INPUT[12]), .INCREMENT(and_4_out), .DECREMENT(or_4_out),
    .SELECTION(SELECTION), .ENABLE(ENABLE), .OUTPUT(OUTPUT[12]));
  or or_5 (or_5_out, OUTPUT[10], or_6_out);
  and and_5 (and_5_out, OUTPUT[10], and_6_out);
  _1_bit_op u_1_bit_op_5 (
    .CLK(CLK), .CLEAR(STATIC_0), .INPUT(INPUT[11]), .INCREMENT(and_5_out), .DECREMENT(or_5_out),
    .SELECTION(SELECTION), .ENABLE(ENABLE), .OUTPUT(OUTPUT[11]));
  _1_bit_op u_1_bit_op_6 (
    .CLK(CLK), .CLEAR(STATIC_0), .INPUT(INPUT[10]), .INCREMENT(and_6_out), .DECREMENT(or_6_out),
    .SELECTION(SELECTION), .ENABLE(ENABLE), .OUTPUT(OUTPUT[10]));
  or or_6 (or_6_out, OUTPUT[9], or_7_out);
  and and_6 (and_6_out, OUTPUT[9], and_7_out);
  _1_bit_op u_1_bit_op_7 (
    .CLK(CLK), .CLEAR(STATIC_0), .INPUT(INPUT[9]), .INCREMENT(and_7_out), .DECREMENT(or_7_out),
    .SELECTION(SELECTION), .ENABLE(ENABLE), .OUTPUT(OUTPUT[9]));
  or or_7 (or_7_out, OUTPUT[8], or_8_out);
  and and_7 (and_7_out, OUTPUT[8], and_8_out);
  _1_bit_op u_1_bit_op_8 (
    .CLK(CLK), .CLEAR(STATIC_0), .INPUT(INPUT[8]), .INCREMENT(and_8_out), .DECREMENT(or_8_out),
    .SELECTION(SELECTION), .ENABLE(ENABLE), .OUTPUT(OUTPUT[8]));
  or or_8 (or_8_out, OUTPUT[7], or_9_out);
  and and_8 (and_8_out, OUTPUT[7], and_9_out);
  _1_bit_op u_1_bit_op_9 (
    .CLK(CLK), .CLEAR(STATIC_0), .INPUT(INPUT[7]), .INCREMENT(and_9_out), .DECREMENT(or_9_out),
    .SELECTION(SELECTION), .ENABLE(ENABLE), .OUTPUT(OUTPUT[7]));
  or or_9 (or_9_out, OUTPUT[6], or_10_out);
  and and_9 (and_9_out, OUTPUT[6], and_10_out);
  _1_bit_op u_1_bit_op_10 (
    .CLK(CLK), .CLEAR(STATIC_0), .INPUT(INPUT[6]), .INCREMENT(and_10_out), .DECREMENT(or_10_out),
    .SELECTION(SELECTION), .ENABLE(ENABLE), .OUTPUT(OUTPUT[6]));
  or or_10 (or_10_out, OUTPUT[5], or_11_out);
  and and_10 (and_10_out, OUTPUT[5], and_11_out);
  or or_11 (or_11_out, OUTPUT[4], or_12_out);
  and and_11 (and_11_out, OUTPUT[4], and_12_out);
  _1_bit_op u_1_bit_op_11 (
    .CLK(CLK), .CLEAR(STATIC_0), .INPUT(INPUT[5]), .INCREMENT(and_11_out), .DECREMENT(or_11_out),
    .SELECTION(SELECTION), .ENABLE(ENABLE), .OUTPUT(OUTPUT[5]));
  or or_12 (or_12_out, OUTPUT[3], or_13_out);
  and and_12 (and_12_out, OUTPUT[3], and_13_out);
  _1_bit_op u_1_bit_op_12 (
    .CLK(CLK), .CLEAR(STATIC_0), .INPUT(INPUT[4]), .INCREMENT(and_12_out), .DECREMENT(or_12_out),
    .SELECTION(SELECTION), .ENABLE(ENABLE), .OUTPUT(OUTPUT[4]));
  or or_13 (or_13_out, OUTPUT[2], or_14_out);
  and and_13 (and_13_out, OUTPUT[2], and_14_out);
  _1_bit_op u_1_bit_op_13 (
    .CLK(CLK), .CLEAR(STATIC_0), .INPUT(INPUT[3]), .INCREMENT(and_13_out), .DECREMENT(or_13_out),
    .SELECTION(SELECTION), .ENABLE(ENABLE), .OUTPUT(OUTPUT[3]));
  _1_bit_op u_1_bit_op_14 (
    .CLK(CLK), .CLEAR(STATIC_0), .INPUT(INPUT[2]), .INCREMENT(and_14_out), .DECREMENT(or_14_out),
    .SELECTION(SELECTION), .ENABLE(ENABLE), .OUTPUT(OUTPUT[2]));
  or or_14 (or_14_out, OUTPUT[1], OUTPUT[0]);
  and and_14 (and_14_out, OUTPUT[1], OUTPUT[0]);
  _1_bit_op u_1_bit_op_15 (
    .CLK(CLK), .CLEAR(STATIC_0), .INPUT(INPUT[1]), .INCREMENT(OUTPUT[0]), .DECREMENT(OUTPUT[0]),
    .SELECTION(SELECTION), .ENABLE(ENABLE), .OUTPUT(OUTPUT[1]));
  _1_bit_op u_1_bit_op_16 (
    .CLK(CLK), .CLEAR(STATIC_0), .INPUT(INPUT[0]), .INCREMENT(STATIC_1), .DECREMENT(STATIC_0),
    .SELECTION(SELECTION), .ENABLE(ENABLE), .OUTPUT(OUTPUT[0]));
  Hex_Digit_Display hex_digit_display_1 (.value(OUTPUT[15:12]));  // open: dp
  Hex_Digit_Display hex_digit_display_2 (.value(INPUT[15:12]));  // open: dp
  Hex_Digit_Display hex_digit_display_3 (.value(OUTPUT[7:4]));  // open: dp
  Hex_Digit_Display hex_digit_display_4 (.value(OUTPUT[11:8]));  // open: dp
  Hex_Digit_Display hex_digit_display_5 (.value(INPUT[7:4]));  // open: dp
  Hex_Digit_Display hex_digit_display_6 (.value(INPUT[11:8]));  // open: dp
  Hex_Digit_Display hex_digit_display_7 (.value(OUTPUT[3:0]));  // open: dp
  Hex_Digit_Display hex_digit_display_8 (.value(INPUT[3:0]));  // open: dp
endmodule
