// Logisim project hw4.circ as structural Verilog: 2 circuits, main circuit main
module main (
  input  [15:0] IR
);

  wire _1MSB, _2MSB, ADD__MOD, and_2_out, and_3_out, and_4_out, and_5_out, and_6_out, and_7_out, and_8_out,
       and_9_out, and_10_out, and_11_out, and_12_out, and_13_out, and_14_out, and_15_out, and_16_out,
       and_17_out, and_18_out, and_19_out, and_20_out, and_21_out, C, CD_STATUS, clock_1_out, clock_2_out,
       clrMEM, decoder_2_out0, decoder_3_out0, Enable2c, F1_M1, F1_M2, F1_M3, F1_M4, F1_M5, F1_M6, F1_M7,
       F1_M8, F1_M9, F1_M10, F1_M11, F1_M12, F1_M13, F1_M14, F1_M15, F1_M16, F1_M17, F1_M18, F1_M19, F1_M20,
       F1_M21, F1_M22, F1_M23, F2_M1, F2_M2, F2_M3, ldMEM, multiplexer_4_out, MuxCSel, N, nL_H, not_1_out,
       not_2_out, not_3_out, not_4_out, not_5_out, not_6_out, not_7_out, not_8_out, not_9_out, not_10_out,
       not_11_out, not_12_out, not_13_out, not_14_out, not_15_out, O, or_1_out, or_2_out, SBR_EN, selMEM,
       strMEM, Z;
  wire [1:0] _1SEL, _2SEL, ADDRESS, CBR, CCD, CF2, FunSel2a, FunSel2b, FunSel2c, multiplexer_5_out,
       multiplexer_11_out, multiplexer_12_out, multiplexer_13_out, MuxASel, MuxBSel, OutASel, OutBSel,
       OutCSel, OutDSel;
  wire [2:0] multiplexer_7_out, multiplexer_10_out, multiplexer_15_out, multiplexer_16_out,
       multiplexer_19_out, multiplexer_21_out, RegSel2b;
  wire [2:1] DESTREG;
  wire [3:0] ALUFunSelCh, decoder_1_out0, FunSelALU, multiplexer_8_out, multiplexer_9_out,
       multiplexer_14_out, multiplexer_17_out, multiplexer_18_out, multiplexer_20_out, multiplexer_22_out,
       RegSel2a;
  wire [4:0] CF1;
  wire [7:0] CAD, CAR, CAR___1, multiplexer_2_out, multiplexer_3_out, SBR_RES;
  wire [15:11] IR_t;

  Decoder #(.select(2), .enable("false")) decoder_1 (
    .out0(decoder_1_out0[0]), .out1(decoder_1_out0[1]), .out2(decoder_1_out0[2]), .out3(decoder_1_out0[3]),
    .sel(DESTREG));
  assign MuxASel = F1_M1 ? 2'b00 : 2'bz;  // Controlled_Buffer controlled_buffer_1
  assign FunSel2a = F1_M1 ? 2'b01 : 2'bz;  // Controlled_Buffer controlled_buffer_2
  assign RegSel2a = F1_M1 ? decoder_1_out0 : 4'bz;  // Controlled_Buffer controlled_buffer_3
  Clock clock_1 (.out(clock_1_out));
  part1_8_main u_CAR (
    .CLK(clock_1_out), .OUTPUT(CAR), .INPUT(multiplexer_2_out), .SELECTION(2'b01), .ENABLE(1'b1));  // open: STATIC_0, STATIC_1
  Hex_Digit_Display hex_digit_display_1 (.value(IR_t[15:12]));  // open: dp
  Hex_Digit_Display hex_digit_display_2 (.value({IR_t[11], DESTREG, ADD__MOD}));  // open: dp
  Hex_Digit_Display hex_digit_display_3 (.value({_1MSB, _1SEL, _2MSB}));  // open: dp
  ROM #(.dataWidth(19)) rom_1 (.addr(CAR), .data({CF1, CF2, CCD, CBR, CAD}));  // open: sel
  hw2part2_main main_1 (
    .IR({IR_t, DESTREG, ADD__MOD, _1MSB, _1SEL, _2MSB, _2SEL, ADDRESS}), .ZCNO_Register({Z, C, N, O}),
    .MuxCSel(MuxCSel), .MuxASel(MuxASel), .OutBSel(OutBSel), .OutASel(OutASel), .FunSel2a(FunSel2a),
    .FunSel2c(FunSel2c), .RegSel2a(RegSel2a), .nL_H(nL_H), .E2c(Enable2c), .MuxBSel(MuxBSel),
    .OutDSel(OutDSel), .FunSelALU(FunSelALU), .OutCSel(OutCSel), .FunSel2b(FunSel2b), .RegSel2b(RegSel2b),
    .strMEM(strMEM), .selMEM(selMEM), .ldMEM(ldMEM), .clrMEM(clrMEM));
  Hex_Digit_Display hex_digit_display_4 (.value({_2SEL, ADDRESS}));  // open: dp
  assign OutDSel = F1_M2 ? 2'b01 : 2'bz;  // Controlled_Buffer controlled_buffer_4
  assign ldMEM = F1_M2 ? 1'b1 : 1'bz;  // Controlled_Buffer controlled_buffer_5
  assign selMEM = F1_M2 ? 1'b1 : 1'bz;  // Controlled_Buffer controlled_buffer_6
  assign strMEM = F1_M2 ? 1'b0 : 1'bz;  // Controlled_Buffer controlled_buffer_7
  assign clrMEM = F1_M2 ? 1'b0 : 1'bz;  // Controlled_Buffer controlled_buffer_8
  assign FunSel2c = F1_M2 ? 2'b11 : 2'bz;  // Controlled_Buffer controlled_buffer_9
  assign nL_H = F1_M2 ? 1'b0 : 1'bz;  // Controlled_Buffer controlled_buffer_10
  assign Enable2c = F1_M2 ? 1'b1 : 1'bz;  // Controlled_Buffer controlled_buffer_11
  Decoder #(.select(5), .enable("false")) decoder_2 (
    .out0(decoder_2_out0), .out1(F1_M1), .out2(F1_M2), .out3(F1_M3), .out4(F1_M4), .out5(F1_M5),
    .out6(F1_M6), .out7(F1_M7), .out8(F1_M8), .out9(F1_M9), .out10(F1_M10), .out11(F1_M11), .out12(F1_M12),
    .out13(F1_M13), .out14(F1_M14), .out15(F1_M15), .out16(F1_M16), .out17(F1_M17), .out18(F1_M18),
    .out19(F1_M19), .out20(F1_M20), .out21(F1_M21), .out22(F1_M22), .out23(F1_M23), .sel(CF1));  // open: out24, out25, out26, out27, out28, out29, out30, out31
  assign OutASel = F1_M3 ? DESTREG : 2'bz;  // Controlled_Buffer controlled_buffer_12
  assign MuxCSel = F1_M3 ? 1'b1 : 1'bz;  // Controlled_Buffer controlled_buffer_13
  assign FunSelALU = F1_M3 ? 4'b0000 : 4'bz;  // Controlled_Buffer controlled_buffer_14
  assign ldMEM = F1_M3 ? 1'b0 : 1'bz;  // Controlled_Buffer controlled_buffer_15
  assign selMEM = F1_M3 ? 1'b1 : 1'bz;  // Controlled_Buffer controlled_buffer_16
  assign strMEM = F1_M3 ? 1'b1 : 1'bz;  // Controlled_Buffer controlled_buffer_17
  assign clrMEM = F1_M3 ? 1'b0 : 1'bz;  // Controlled_Buffer controlled_buffer_18
  assign OutDSel = F1_M3 ? 2'b01 : 2'bz;  // Controlled_Buffer controlled_buffer_19
  Multiplexer #(.select(2), .enable("false")) multiplexer_1 (
    .in0(1'b1), .in1(ADD__MOD), .in2(Z), .in3(1'b1), .out(CD_STATUS), .sel(CCD));
  Multiplexer #(.width(8), .enable("false")) multiplexer_2 (
    .in0(CAR___1), .in1(multiplexer_3_out), .out(multiplexer_2_out), .sel(CD_STATUS));
  Decoder #(.select(2), .enable("false")) decoder_3 (
    .out0(decoder_3_out0), .out1(F2_M1), .out2(F2_M2), .out3(F2_M3), .sel(CF2));
  and and_1 (SBR_EN, multiplexer_4_out, CD_STATUS);
  assign MuxBSel = F1_M4 ? 2'b01 : 2'bz;  // Controlled_Buffer controlled_buffer_20
  assign RegSel2b = F1_M4 ? 3'b001 : 3'bz;  // Controlled_Buffer controlled_buffer_21
  assign FunSel2b = F1_M4 ? 2'b01 : 2'bz;  // Controlled_Buffer controlled_buffer_22
  Multiplexer #(.select(2), .width(8), .enable("false")) multiplexer_3 (
    .in0(CAD), .in1(CAD), .in2(SBR_RES), .in3({1'b1, IR_t, 2'b00}), .out(multiplexer_3_out), .sel(CBR));
  Multiplexer #(.select(2), .enable("false")) multiplexer_4 (
    .in0(1'b0), .in1(1'b1), .in2(1'b0), .in3(1'b0), .out(multiplexer_4_out), .sel(CBR));
  Multiplexer #(.select(2), .width(2), .enable("false")) multiplexer_5 (
    .in0(2'b00), .in1(2'b00), .in2(2'b01), .in3(2'b10), .out(multiplexer_5_out), .sel({DESTREG[1], ADD__MOD}));
  assign FunSelALU = F1_M5 ? 4'b0000 : 4'bz;  // Controlled_Buffer controlled_buffer_23
  assign OutCSel = F1_M5 ? multiplexer_5_out : 2'bz;  // Controlled_Buffer controlled_buffer_24
  not not_1 (not_1_out, DESTREG[2]);
  assign MuxCSel = F1_M5 ? not_1_out : 1'bz;  // Controlled_Buffer controlled_buffer_25
  assign OutASel = F1_M5 ? {DESTREG[1], ADD__MOD} : 2'bz;  // Controlled_Buffer controlled_buffer_26
  assign ldMEM = F1_M5 ? 1'b0 : 1'bz;  // Controlled_Buffer controlled_buffer_27
  assign selMEM = F1_M5 ? 1'b1 : 1'bz;  // Controlled_Buffer controlled_buffer_28
  assign strMEM = F1_M5 ? 1'b0 : 1'bz;  // Controlled_Buffer controlled_buffer_29
  assign clrMEM = F1_M5 ? 1'b0 : 1'bz;  // Controlled_Buffer controlled_buffer_30
  Multiplexer #(.select(4), .width(4), .enable("false")) multiplexer_6 (
    .in0(4'b0000), .in1(4'b0010), .in2(4'b1010), .in3(4'b1011), .in4(4'b0100), .in5(4'b0110), .in6(4'b0111),
    .in7(4'b1000), .out(ALUFunSelCh), .sel(CF1[3:0]));  // open: in8, in9, in10, in11, in12, in13, in14, in15
  Incrementer INCREMENTER (.OUTPUT(CAR___1), .INPUT(CAR));
  Clock clock_2 (.out(clock_2_out));
  part1_8_main SBR (
    .CLK(clock_2_out), .OUTPUT(SBR_RES), .INPUT(CAR___1), .SELECTION(2'b01), .ENABLE(SBR_EN));  // open: STATIC_0, STATIC_1
  assign OutDSel = F1_M6 ? 2'b10 : 2'bz;  // Controlled_Buffer controlled_buffer_31
  assign ldMEM = F1_M6 ? 1'b0 : 1'bz;  // Controlled_Buffer controlled_buffer_32
  assign selMEM = F1_M6 ? 1'b1 : 1'bz;  // Controlled_Buffer controlled_buffer_33
  assign strMEM = F1_M6 ? 1'b1 : 1'bz;  // Controlled_Buffer controlled_buffer_34
  assign clrMEM = F1_M6 ? 1'b0 : 1'bz;  // Controlled_Buffer controlled_buffer_35
  assign OutCSel = F1_M6 ? 2'b00 : 2'bz;  // Controlled_Buffer controlled_buffer_36
  assign MuxASel = F1_M6 ? 2'b10 : 2'bz;  // Controlled_Buffer controlled_buffer_37
  assign MuxCSel = F1_M6 ? 1'b0 : 1'bz;  // Controlled_Buffer controlled_buffer_38
  assign FunSelALU = F1_M6 ? 4'b0000 : 4'bz;  // Controlled_Buffer controlled_buffer_39
  not not_2 (not_2_out, _1MSB);
  Multiplexer #(.select(2), .width(3), .enable("false")) multiplexer_7 (
    .in0(3'b001), .in1(3'b001), .in2(3'b010), .in3(3'b100), .out(multiplexer_7_out),
    .sel({DESTREG[1], ADD__MOD}));
  not not_3 (not_3_out, DESTREG[2]);
  Multiplexer #(.select(2), .width(4), .enable("false")) multiplexer_8 (
    .in0(4'b0001), .in1(4'b0010), .in2(4'b0100), .in3(4'b1000), .out(multiplexer_8_out),
    .sel({DESTREG[1], ADD__MOD}));
  not not_4 (not_4_out, DESTREG[2]);
  not not_5 (not_5_out, _1MSB);
  Multiplexer #(.select(2), .width(4), .enable("false")) multiplexer_9 (
    .in0(4'b0001), .in1(4'b0010), .in2(4'b0100), .in3(4'b1000), .out(multiplexer_9_out),
    .sel({DESTREG[1], ADD__MOD}));
  Multiplexer #(.select(2), .width(3), .enable("false")) multiplexer_10 (
    .in0(3'b001), .in1(3'b001), .in2(3'b010), .in3(3'b100), .out(multiplexer_10_out),
    .sel({DESTREG[1], ADD__MOD}));
  Multiplexer #(.select(2), .width(2), .enable("false")) multiplexer_11 (
    .in0(2'b00), .in1(2'b00), .in2(2'b01), .in3(2'b10), .out(multiplexer_11_out), .sel(_1SEL));
  or or_1 (or_1_out, F1_M18, F1_M19, F1_M16, F1_M17);
  and and_2 (and_2_out, DESTREG[2], not_2_out);
  and and_3 (and_3_out, and_2_out, or_1_out);
  assign OutASel = and_3_out ? _1SEL : 2'bz;  // Controlled_Buffer controlled_buffer_40
  assign MuxBSel = and_3_out ? 2'b11 : 2'bz;  // Controlled_Buffer controlled_buffer_41
  assign FunSel2b = and_3_out ? 2'b01 : 2'bz;  // Controlled_Buffer controlled_buffer_42
  assign RegSel2b = and_3_out ? multiplexer_7_out : 3'bz;  // Controlled_Buffer controlled_buffer_43
  assign FunSelALU = and_3_out ? ALUFunSelCh : 4'bz;  // Controlled_Buffer controlled_buffer_44
  assign MuxCSel = and_3_out ? 1'b1 : 1'bz;  // Controlled_Buffer controlled_buffer_45
  and and_4 (and_4_out, not_3_out, _1MSB);
  and and_5 (and_5_out, and_4_out, or_1_out);
  assign OutCSel = and_5_out ? _1SEL : 2'bz;  // Controlled_Buffer controlled_buffer_46
  assign FunSelALU = and_5_out ? ALUFunSelCh : 4'bz;  // Controlled_Buffer controlled_buffer_47
  assign MuxCSel = and_5_out ? 1'b0 : 1'bz;  // Controlled_Buffer controlled_buffer_48
  assign MuxASel = and_5_out ? 2'b11 : 2'bz;  // Controlled_Buffer controlled_buffer_49
  assign FunSel2a = and_5_out ? 2'b01 : 2'bz;  // Controlled_Buffer controlled_buffer_50
  assign RegSel2a = and_5_out ? multiplexer_8_out : 4'bz;  // Controlled_Buffer controlled_buffer_51
  and and_6 (and_6_out, not_4_out, not_5_out);
  and and_7 (and_7_out, and_6_out, or_1_out);
  assign MuxCSel = and_7_out ? 1'b1 : 1'bz;  // Controlled_Buffer controlled_buffer_52
  assign MuxASel = and_7_out ? 2'b11 : 2'bz;  // Controlled_Buffer controlled_buffer_53
  assign FunSel2a = and_7_out ? 2'b01 : 2'bz;  // Controlled_Buffer controlled_buffer_54
  assign RegSel2a = and_7_out ? multiplexer_9_out : 4'bz;  // Controlled_Buffer controlled_buffer_55
  assign OutASel = and_7_out ? _1SEL : 2'bz;  // Controlled_Buffer controlled_buffer_56
  assign FunSelALU = and_7_out ? ALUFunSelCh : 4'bz;  // Controlled_Buffer controlled_buffer_57
  and and_8 (and_8_out, DESTREG[2], _1MSB);
  and and_9 (and_9_out, and_8_out, or_1_out);
  assign MuxCSel = and_9_out ? 1'b0 : 1'bz;  // Controlled_Buffer controlled_buffer_58
  assign MuxASel = and_9_out ? 2'b10 : 2'bz;  // Controlled_Buffer controlled_buffer_59
  assign FunSel2b = and_9_out ? 2'b01 : 2'bz;  // Controlled_Buffer controlled_buffer_60
  assign RegSel2b = and_9_out ? multiplexer_10_out : 3'bz;  // Controlled_Buffer controlled_buffer_61
  assign OutCSel = and_9_out ? multiplexer_11_out : 2'bz;  // Controlled_Buffer controlled_buffer_62
  assign FunSelALU = and_9_out ? ALUFunSelCh : 4'bz;  // Controlled_Buffer controlled_buffer_63
  assign MuxBSel = and_9_out ? 2'b11 : 2'bz;  // Controlled_Buffer controlled_buffer_64
  not not_6 (not_6_out, DESTREG[2]);
  not not_7 (not_7_out, _1MSB);
  not not_8 (not_8_out, _2MSB);
  not not_9 (not_9_out, _1MSB);
  not not_10 (not_10_out, _2MSB);
  not not_11 (not_11_out, _2MSB);
  Multiplexer #(.select(2), .width(2), .enable("false")) multiplexer_12 (
    .in0(2'b00), .in1(2'b00), .in2(2'b01), .in3(2'b10), .out(multiplexer_12_out), .sel(_1SEL));
  not not_12 (not_12_out, DESTREG[2]);
  not not_13 (not_13_out, _2MSB);
  Multiplexer #(.select(2), .width(2), .enable("false")) multiplexer_13 (
    .in0(2'b00), .in1(2'b00), .in2(2'b01), .in3(2'b10), .out(multiplexer_13_out), .sel(_1SEL));
  and and_10 (and_10_out, not_6_out, not_7_out, not_8_out);
  Multiplexer #(.select(2), .width(4), .enable("false")) multiplexer_14 (
    .in0(4'b0001), .in1(4'b0010), .in2(4'b0100), .in3(4'b1000), .out(multiplexer_14_out),
    .sel({DESTREG[1], ADD__MOD}));
  and and_11 (and_11_out, DESTREG[2], not_9_out, not_10_out);
  Multiplexer #(.select(2), .width(3), .enable("false")) multiplexer_15 (
    .in0(3'b001), .in1(3'b001), .in2(3'b010), .in3(3'b100), .out(multiplexer_15_out),
    .sel({DESTREG[1], ADD__MOD}));
  and and_12 (and_12_out, DESTREG[2], _1MSB, not_11_out);
  Multiplexer #(.select(2), .width(3), .enable("false")) multiplexer_16 (
    .in0(3'b001), .in1(3'b001), .in2(3'b010), .in3(3'b100), .out(multiplexer_16_out),
    .sel({DESTREG[1], ADD__MOD}));
  and and_13 (and_13_out, not_12_out, _1MSB, not_13_out);
  Multiplexer #(.select(2), .width(4), .enable("false")) multiplexer_17 (
    .in0(4'b0001), .in1(4'b0010), .in2(4'b0100), .in3(4'b1000), .out(multiplexer_17_out),
    .sel({DESTREG[1], ADD__MOD}));
  or or_2 (or_2_out, F1_M22, F1_M21, F1_M20, F1_M23);
  and and_14 (and_14_out, and_10_out, or_2_out);
  assign OutASel = and_14_out ? _1SEL : 2'bz;  // Controlled_Buffer controlled_buffer_65
  assign OutBSel = and_14_out ? _2SEL : 2'bz;  // Controlled_Buffer controlled_buffer_66
  assign MuxCSel = and_14_out ? 1'b1 : 1'bz;  // Controlled_Buffer controlled_buffer_67
  assign FunSelALU = and_14_out ? ALUFunSelCh : 4'bz;  // Controlled_Buffer controlled_buffer_68
  assign MuxASel = and_14_out ? 2'b11 : 2'bz;  // Controlled_Buffer controlled_buffer_69
  assign FunSel2a = and_14_out ? 2'b01 : 2'bz;  // Controlled_Buffer controlled_buffer_70
  assign RegSel2a = and_14_out ? multiplexer_14_out : 4'bz;  // Controlled_Buffer controlled_buffer_71
  and and_15 (and_15_out, and_11_out, or_2_out);
  assign OutASel = and_15_out ? _1SEL : 2'bz;  // Controlled_Buffer controlled_buffer_72
  assign OutBSel = and_15_out ? _2SEL : 2'bz;  // Controlled_Buffer controlled_buffer_73
  assign MuxCSel = and_15_out ? 1'b1 : 1'bz;  // Controlled_Buffer controlled_buffer_74
  assign FunSelALU = and_15_out ? ALUFunSelCh : 4'bz;  // Controlled_Buffer controlled_buffer_75
  assign MuxASel = and_15_out ? 2'b11 : 2'bz;  // Controlled_Buffer controlled_buffer_76
  assign FunSel2a = and_15_out ? 2'b01 : 2'bz;  // Controlled_Buffer controlled_buffer_77
  assign RegSel2b = and_15_out ? multiplexer_15_out : 3'bz;  // Controlled_Buffer controlled_buffer_78
  and and_16 (and_16_out, and_12_out, or_2_out);
  assign OutCSel = and_16_out ? multiplexer_12_out : 2'bz;  // Controlled_Buffer controlled_buffer_79
  assign OutBSel = and_16_out ? _2SEL : 2'bz;  // Controlled_Buffer controlled_buffer_80
  assign MuxASel = and_16_out ? 2'b10 : 2'bz;  // Controlled_Buffer controlled_buffer_81
  assign FunSelALU = and_16_out ? ALUFunSelCh : 4'bz;  // Controlled_Buffer controlled_buffer_82
  assign MuxCSel = and_16_out ? 1'b0 : 1'bz;  // Controlled_Buffer controlled_buffer_83
  assign MuxBSel = and_16_out ? 2'b11 : 2'bz;  // Controlled_Buffer controlled_buffer_84
  assign FunSel2b = and_16_out ? 2'b01 : 2'bz;  // Controlled_Buffer controlled_buffer_85
  assign RegSel2b = and_16_out ? multiplexer_16_out : 3'bz;  // Controlled_Buffer controlled_buffer_86
  and and_17 (and_17_out, and_13_out, or_2_out);
  assign OutCSel = and_17_out ? multiplexer_13_out : 2'bz;  // Controlled_Buffer controlled_buffer_87
  assign OutBSel = and_17_out ? _2SEL : 2'bz;  // Controlled_Buffer controlled_buffer_88
  assign MuxASel = and_17_out ? 2'b11 : 2'bz;  // Controlled_Buffer controlled_buffer_89
  assign FunSelALU = and_17_out ? ALUFunSelCh : 4'bz;  // Controlled_Buffer controlled_buffer_90
  assign MuxCSel = and_17_out ? 1'b0 : 1'bz;  // Controlled_Buffer controlled_buffer_91
  assign FunSel2a = and_17_out ? 2'b01 : 2'bz;  // Controlled_Buffer controlled_buffer_92
  assign RegSel2a = and_17_out ? multiplexer_17_out : 4'bz;  // Controlled_Buffer controlled_buffer_93
  not not_14 (not_14_out, DESTREG[2]);
  Multiplexer #(.select(2), .width(4), .enable("false")) multiplexer_18 (
    .in0(4'b0001), .in1(4'b0010), .in2(4'b0100), .in3(4'b1000), .out(multiplexer_18_out),
    .sel({DESTREG[1], ADD__MOD}));
  Multiplexer #(.select(2), .width(3), .enable("false")) multiplexer_19 (
    .in0(3'b001), .in1(3'b001), .in2(3'b010), .in3(3'b100), .out(multiplexer_19_out),
    .sel({DESTREG[1], ADD__MOD}));
  and and_18 (and_18_out, not_14_out, F1_M9);
  assign FunSel2a = and_18_out ? 2'b10 : 2'bz;  // Controlled_Buffer controlled_buffer_94
  assign RegSel2a = and_18_out ? multiplexer_18_out : 4'bz;  // Controlled_Buffer controlled_buffer_95
  and and_19 (and_19_out, DESTREG[2], F1_M9);
  assign FunSel2b = and_19_out ? 2'b10 : 2'bz;  // Controlled_Buffer controlled_buffer_96
  assign RegSel2b = and_19_out ? multiplexer_19_out : 3'bz;  // Controlled_Buffer controlled_buffer_97
  Multiplexer #(.select(2), .width(4), .enable("false")) multiplexer_20 (
    .in0(4'b0001), .in1(4'b0010), .in2(4'b0100), .in3(4'b1000), .out(multiplexer_20_out),
    .sel({DESTREG[1], ADD__MOD}));
  Multiplexer #(.select(2), .width(3), .enable("false")) multiplexer_21 (
    .in0(3'b001), .in1(3'b001), .in2(3'b010), .in3(3'b100), .out(multiplexer_21_out),
    .sel({DESTREG[1], ADD__MOD}));
  not not_15 (not_15_out, DESTREG[2]);
  and and_20 (and_20_out, not_15_out, F1_M10);
  assign FunSel2a = and_20_out ? 2'b11 : 2'bz;  // Controlled_Buffer controlled_buffer_98
  assign RegSel2a = and_20_out ? multiplexer_20_out : 4'bz;  // Controlled_Buffer controlled_buffer_99
  and and_21 (and_21_out, DESTREG[2], F1_M10);
  assign FunSel2b = and_21_out ? 2'b11 : 2'bz;  // Controlled_Buffer controlled_buffer_100
  assign RegSel2b = and_21_out ? multiplexer_21_out : 3'bz;  // Controlled_Buffer controlled_buffer_101
  assign MuxBSel = F1_M11 ? 2'b10 : 2'bz;  // Controlled_Buffer controlled_buffer_102
  assign RegSel2b = F1_M11 ? 3'b001 : 3'bz;  // Controlled_Buffer controlled_buffer_103
  assign FunSel2b = F1_M11 ? 2'b01 : 2'bz;  // Controlled_Buffer controlled_buffer_104
  assign OutDSel = F1_M11 ? 2'b10 : 2'bz;  // Controlled_Buffer controlled_buffer_105
  assign ldMEM = F1_M11 ? 1'b1 : 1'bz;  // Controlled_Buffer controlled_buffer_106
  assign selMEM = F1_M11 ? 1'b1 : 1'bz;  // Controlled_Buffer controlled_buffer_107
  assign strMEM = F1_M11 ? 1'b0 : 1'bz;  // Controlled_Buffer controlled_buffer_108
  assign clrMEM = F1_M11 ? 1'b0 : 1'bz;  // Controlled_Buffer controlled_buffer_109
  assign OutDSel = F1_M12 ? 2'b10 : 2'bz;  // Controlled_Buffer controlled_buffer_110
  assign ldMEM = F1_M12 ? 1'b0 : 1'bz;  // Controlled_Buffer controlled_buffer_111
  assign selMEM = F1_M12 ? 1'b1 : 1'bz;  // Controlled_Buffer controlled_buffer_112
  assign strMEM = F1_M12 ? 1'b1 : 1'bz;  // Controlled_Buffer controlled_buffer_113
  assign clrMEM = F1_M12 ? 1'b0 : 1'bz;  // Controlled_Buffer controlled_buffer_114
  assign MuxCSel = F1_M12 ? 1'b1 : 1'bz;  // Controlled_Buffer controlled_buffer_115
  assign FunSelALU = F1_M12 ? 4'b0000 : 4'bz;  // Controlled_Buffer controlled_buffer_116
  assign OutASel = F1_M12 ? _1SEL : 2'bz;  // Controlled_Buffer controlled_buffer_117
  assign OutDSel = F1_M13 ? 2'b10 : 2'bz;  // Controlled_Buffer controlled_buffer_118
  Multiplexer #(.select(2), .width(4), .enable("false")) multiplexer_22 (
    .in0(4'b0001), .in1(4'b0010), .in2(4'b0100), .in3(4'b1000), .out(multiplexer_22_out),
    .sel({DESTREG[1], ADD__MOD}));
  assign RegSel2a = F1_M13 ? multiplexer_22_out : 4'bz;  // Controlled_Buffer controlled_buffer_119
  assign FunSel2a = F1_M13 ? 2'b01 : 2'bz;  // Controlled_Buffer controlled_buffer_120
  assign MuxASel = F1_M13 ? 2'b01 : 2'bz;  // Controlled_Buffer controlled_buffer_121
  assign ldMEM = F1_M13 ? 1'b1 : 1'bz;  // Controlled_Buffer controlled_buffer_122
  assign selMEM = F1_M13 ? 1'b1 : 1'bz;  // Controlled_Buffer controlled_buffer_123
  assign strMEM = F1_M13 ? 1'b0 : 1'bz;  // Controlled_Buffer controlled_buffer_124
  assign clrMEM = F1_M13 ? 1'b0 : 1'bz;  // Controlled_Buffer controlled_buffer_125
  assign OutASel = F1_M13 ? {DESTREG[1], ADD__MOD} : 2'bz;  // Controlled_Buffer controlled_buffer_126
  assign OutDSel = F1_M14 ? 2'b00 : 2'bz;  // Controlled_Buffer controlled_buffer_127
  assign ldMEM = F1_M14 ? 1'b1 : 1'bz;  // Controlled_Buffer controlled_buffer_128
  assign selMEM = F1_M14 ? 1'b1 : 1'bz;  // Controlled_Buffer controlled_buffer_129
  assign strMEM = F1_M14 ? 1'b0 : 1'bz;  // Controlled_Buffer controlled_buffer_130
  assign clrMEM = F1_M14 ? 1'b0 : 1'bz;  // Controlled_Buffer controlled_buffer_131
  assign nL_H = F1_M14 ? 1'b1 : 1'bz;  // Controlled_Buffer controlled_buffer_132
  assign Enable2c = F1_M14 ? 1'b1 : 1'bz;  // Controlled_Buffer controlled_buffer_133
  assign FunSel2c = F1_M14 ? 2'b11 : 2'bz;  // Controlled_Buffer controlled_buffer_134
  assign OutDSel = F1_M15 ? 2'b00 : 2'bz;  // Controlled_Buffer controlled_buffer_135
  assign ldMEM = F1_M15 ? 1'b1 : 1'bz;  // Controlled_Buffer controlled_buffer_136
  assign selMEM = F1_M15 ? 1'b1 : 1'bz;  // Controlled_Buffer controlled_buffer_137
  assign strMEM = F1_M15 ? 1'b0 : 1'bz;  // Controlled_Buffer controlled_buffer_138
  assign clrMEM = F1_M15 ? 1'b0 : 1'bz;  // Controlled_Buffer controlled_buffer_139
  assign nL_H = F1_M15 ? 1'b0 : 1'bz;  // Controlled_Buffer controlled_buffer_140
  assign Enable2c = F1_M15 ? 1'b1 : 1'bz;  // Controlled_Buffer controlled_buffer_141
  assign FunSel2c = F1_M15 ? 2'b11 : 2'bz;  // Controlled_Buffer controlled_buffer_142
  assign RegSel2b = F2_M1 ? 3'b001 : 3'bz;  // Controlled_Buffer controlled_buffer_143
  assign FunSel2b = F2_M1 ? 2'b10 : 2'bz;  // Controlled_Buffer controlled_buffer_144
  assign RegSel2b = F2_M2 ? 3'b100 : 3'bz;  // Controlled_Buffer controlled_buffer_145
  assign FunSel2b = F2_M2 ? 2'b10 : 2'bz;  // Controlled_Buffer controlled_buffer_146
  assign RegSel2b = F2_M3 ? 3'b100 : 3'bz;  // Controlled_Buffer controlled_buffer_147
  assign FunSel2b = F2_M3 ? 2'b11 : 2'bz;  // Controlled_Buffer controlled_buffer_148

  // Other names for the same wires on the sheet: IR_t[10:0] = {DESTREG, ADD__MOD, _1MSB, _1SEL, _2MSB, _2SEL, ADDRESS};
  //   ADDRESS[7:2] = {_1MSB, _1SEL, _2MSB, _2SEL}; SRCREG2[2:0] = {_2MSB, _2SEL}; SRCREG1[2:0] = {_1MSB, _1SEL};
  //   DESTREG[0] = ADD__MOD; DSEL[1:0] = {DESTREG[1], ADD__MOD}; REGSEL[1:0] = DESTREG; DMSB = DESTREG[2];
  //   MAP[6:2] = IR_t; OPCODE[4:0] = IR_t; ZCNO[3:0] = {Z, C, N, O}

  // Notes on the sheet:
  //   MICRO-OPS
  //   READ: Rx <- IR(0-7)
  //   Load
  //   Enable
  //   CURRENT INSTRUCTION
  //   CONTROL MEMORY
  //   contents of rom_1 (hex, n*v repeats v):
  //   39001 3d302 0 0 8205 123*0 504 4000 0 0 c000 0 0 0 40000 0 0 0 3008d 0 0 0 91 34000 0 0 50000 0 0 0
  //   54000 0 0 0 2809d 14000 0 0 240a1 14000 0 0 58000 0 0 0 5c000 0 0 0 44000 0 0 0 48000 0 0 0 4c000 0
  //   0 0 10000 0 0 0 8b8 0 0 0 800 b8 0 0 1b0c5 10000 0 0 20c9 2c000
  //   MREAD: Rx <- M[AR]
  //   STORE: M[AR] <- Rx
  //   MICRO-OP DECODERS
  //   BRANCH: PC <- Value
  //   FLAG: ALU <- Reg
  //   ALU Decoder
  //   Load
  //   SETSTACK: M[SP] <- PC
  //   2b <- 2a
  //   2a <- 2b
  //   2a <- 2a
  //   2b <- 2b
  //   ALUA: Reg <- ALU[Reg]
  //   Used for 0x02 - MOV
  //   0x0B - NOT
  //   0x0C - LSL
  //   0x0D - LSR
  //   a <- a + a
  //   b <- a + a
  //   b <- b + a
  //   a <- b + a
  //   ALUAB: Reg <- ALU[Reg, Reg]
  //   Used for 0x05 - ADD
  //   0x06 - SUB
  //   0x09 - AND
  //   0x0A - OR
  //   INCR: Reg <- Reg + 1
  //   DECR: Reg <- Reg - 1
  //   GETSTACK: PC <- M[SP]
  //   CHNGSTACK: M[SP] <- Rx
  //   STRSTACK: Rx <- M[SP]
  //   PCTIRH: IR(8-15) <- M[PC]
  //   PCTIRL: IR(0-7) <- M[PC]
  //   INCPC: PC <- PC + 1
  //   INCSTACK: SP <- SP + 1
  //   DECSTACK: SP <- SP - 1
endmodule

module Incrementer (
  input  [7:0] INPUT,
  output [7:0] OUTPUT
);

  Adder adder_1 (.a(INPUT), .b(8'h1), .out(OUTPUT));  // open: cin, cout
endmodule
