// Logisim project part2a.circ as structural Verilog: 3 circuits, main circuit main
module main (
  input  [3:0] RegSel,
  input  [1:0] FunSel,
  input  [1:0] OutASel,
  input  [1:0] OutBSel,
  input  [7:0] INPUT,
  output [7:0] OutA,
  output [7:0] OutB
);

  wire clock_1_out;
  wire [7:0] R0_output, r1_output, R2_output, R3_output;

  Clock clock_1 (.out(clock_1_out));
  Hex_Digit_Display hex_digit_display_1 (.value(INPUT[3:0]));  // open: dp
  Hex_Digit_Display hex_digit_display_2 (.value(INPUT[7:4]));  // open: dp
  _8_bit_register R3 (
    .STATIC_0(1'b0), .STATIC_1(1'b1), .CLK(clock_1_out), .OUTPUT(R3_output), .INPUT(INPUT),
    .SELECTION(FunSel), .ENABLE(RegSel[3]));
  _8_bit_register R2 (
    .STATIC_0(1'b0), .STATIC_1(1'b1), .CLK(clock_1_out), .OUTPUT(R2_output), .INPUT(INPUT),
    .SELECTION(FunSel), .ENABLE(RegSel[2]));
  _8_bit_register r1 (
    .STATIC_0(1'b0), .STATIC_1(1'b1), .CLK(clock_1_out), .OUTPUT(r1_output), .INPUT(INPUT),
    .SELECTION(FunSel), .ENABLE(RegSel[1]));
  _8_bit_register R0 (
    .STATIC_0(1'b0), .STATIC_1(1'b1), .CLK(clock_1_out), .OUTPUT(R0_output), .INPUT(INPUT),
    .SELECTION(FunSel), .ENABLE(RegSel[0]));
  Multiplexer #(.select(2), .width(8), .enable("false")) multiplexer_1 (
    .in0(R0_output), .in1(r1_output), .in2(R2_output), .in3(R3_output), .out(OutA), .sel(OutASel));
  Multiplexer #(.select(2), .width(8), .enable("false")) multiplexer_2 (
    .in0(R0_output), .in1(r1_output), .in2(R2_output), .in3(R3_output), .out(OutB), .sel(OutBSel));
  Hex_Digit_Display hex_digit_display_3 (.value(OutA[7:4]));  // open: dp
  Hex_Digit_Display hex_digit_display_4 (.value(OutA[3:0]));  // open: dp
  Hex_Digit_Display hex_digit_display_5 (.value(OutB[3:0]));  // open: dp
  Hex_Digit_Display hex_digit_display_6 (.value(OutB[7:4]));  // open: dp
endmodule

module _8_bit_register (
  input  CLK,
  input  [1:0] SELECTION,
  input  ENABLE,
  input  STATIC_0,
  input  STATIC_1,
  input  [7:0] INPUT,
  output [7:0] OUTPUT
);

  wire and_1_out, and_2_out, and_3_out, and_4_out, and_5_out, and_6_out, or_1_out, or_2_out, or_3_out,
       or_4_out, or_5_out, or_6_out;

  Clock clock_1 ();  // open: out
  _1_bit_op u_1_bit_op_1 (
    .CLK(CLK), .CLEAR(STATIC_0), .INPUT(INPUT[7]), .INCREMENT(and_1_out), .DECREMENT(or_1_out),
    .SELECTION(SELECTION), .ENABLE(ENABLE), .OUTPUT(OUTPUT[7]));
  or or_1 (or_1_out, OUTPUT[6], or_2_out);
  and and_1 (and_1_out, OUTPUT[6], and_2_out);
  _1_bit_op u_1_bit_op_2 (
    .CLK(CLK), .CLEAR(STATIC_0), .INPUT(INPUT[6]), .INCREMENT(and_2_out), .DECREMENT(or_2_out),
    .SELECTION(SELECTION), .ENABLE(ENABLE), .OUTPUT(OUTPUT[6]));
  or or_2 (or_2_out, OUTPUT[5], or_3_out);
  and and_2 (and_2_out, OUTPUT[5], and_3_out);
  _1_bit_op u_1_bit_op_3 (
    .CLK(CLK), .CLEAR(STATIC_0), .INPUT(INPUT[5]), .INCREMENT(and_3_out), .DECREMENT(or_3_out),
    .SELECTION(SELECTION), .ENABLE(ENABLE), .OUTPUT(OUTPUT[5]));
  or or_3 (or_3_out, OUTPUT[4], or_4_out);
  and and_3 (and_3_out, OUTPUT[4], and_4_out);
  or or_4 (or_4_out, OUTPUT[3], or_5_out);
  and and_4 (and_4_out, OUTPUT[3], and_5_out);
  _1_bit_op u_1_bit_op_4 (
    .CLK(CLK), .CLEAR(STATIC_0), .INPUT(INPUT[4]), .INCREMENT(and_4_out), .DECREMENT(or_4_out),
    .SELECTION(SELECTION), .ENABLE(ENABLE), .OUTPUT(OUTPUT[4]));
  or or_5 (or_5_out, OUTPUT[2], or_6_out);
  and and_5 (and_5_out, OUTPUT[2], and_6_out);
  _1_bit_op u_1_bit_op_5 (
    .CLK(CLK), .CLEAR(STATIC_0), .INPUT(INPUT[3]), .INCREMENT(and_5_out), .DECREMENT(or_5_out),
    .SELECTION(SELECTION), .ENABLE(ENABLE), .OUTPUT(OUTPUT[3]));
  or or_6 (or_6_out, OUTPUT[1], OUTPUT[0]);
  and and_6 (and_6_out, OUTPUT[1], OUTPUT[0]);
  _1_bit_op u_1_bit_op_6 (
    .CLK(CLK), .CLEAR(STATIC_0), .INPUT(INPUT[2]), .INCREMENT(and_6_out), .DECREMENT(or_6_out),
    .SELECTION(SELECTION), .ENABLE(ENABLE), .OUTPUT(OUTPUT[2]));
  _1_bit_op u_1_bit_op_7 (
    .CLK(CLK), .CLEAR(STATIC_0), .INPUT(INPUT[1]), .INCREMENT(OUTPUT[0]), .DECREMENT(OUTPUT[0]),
    .SELECTION(SELECTION), .ENABLE(ENABLE), .OUTPUT(OUTPUT[1]));
  _1_bit_op u_1_bit_op_8 (
    .CLK(CLK), .CLEAR(STATIC_0), .INPUT(INPUT[0]), .INCREMENT(STATIC_1), .DECREMENT(STATIC_0),
    .SELECTION(SELECTION), .ENABLE(ENABLE), .OUTPUT(OUTPUT[0]));
  Hex_Digit_Display hex_digit_display_1 (.value(OUTPUT[7:4]));  // open: dp
  Hex_Digit_Display hex_digit_display_2 (.value(OUTPUT[3:0]));  // open: dp
  Hex_Digit_Display hex_digit_display_3 (.value(INPUT[7:4]));  // open: dp
  Hex_Digit_Display hex_digit_display_4 (.value(INPUT[3:0]));  // open: dp
endmodule

module _1_bit_op (
  input  CLK,
  input  CLEAR,
  input  INPUT,
  input  [1:0] SELECTION,
  input  ENABLE,
  input  DECREMENT,
  input  INCREMENT,
  output OUTPUT
);

  wire multiplexer_1_out, xnor_1_out, xor_1_out;

  xor xor_1 (xor_1_out, INCREMENT, OUTPUT);
  xnor xnor_1 (xnor_1_out, DECREMENT, OUTPUT);
  Multiplexer #(.select(2), .enable("false")) multiplexer_1 (
    .in0(CLEAR), .in1(INPUT), .in2(xor_1_out), .in3(xnor_1_out), .out(multiplexer_1_out), .sel(SELECTION));
  D_Flip_Flop d_ff_1 (.clk(CLK), .D(multiplexer_1_out), .Q(OUTPUT), .en(ENABLE));  // open: Qn, preset, reset

  // Notes on the sheet:
  //   Bit n XNOR (Bit n-1 OR (Bit n-2 OR (... OR Bit 0)))
  //   Bit n XOR (Bit n-1 AND (Bit n-2 AND (... AND Bit 0)))
endmodule
