// Logisim project hw2part1.circ as structural Verilog: 8 circuits, main circuit Main
module ALU (
  input  [7:0] A,
  input  [7:0] B,
  input  Cin,
  input  [3:0] FunSel,
  output [3:0] OutFlag,
  output [7:0] OutALU
);

  wire arithmetic_1_cout, arithmetic_1_overflow, arithmetic_shift_1_overflow, circular_shift_1_cout,
       circular_shift_1_overflow, decoder_1_out4, decoder_1_out5, decoder_1_out6, decoder_1_out10,
       decoder_1_out12, decoder_1_out14, decoder_1_out15, logic_shift_1_carry, multiplexer_2_out,
       multiplexer_3_out, not_3_out, not_4_out, or_1_out, or_2_out, or_3_out, xor_1_out;
  wire [7:0] arithmetic_1_output, arithmetic_shift_1_output, circular_shift_1_output, logic_shift_1_output,
       logical_1_and, logical_1_or, logical_1_xor, not_1_out, not_2_out;

  Hex_Digit_Display hex_digit_display_1 (.value(A[7:4]));  // open: dp
  Decoder #(.select(4), .enable("false")) decoder_1 (
    .out4(decoder_1_out4), .out5(decoder_1_out5), .out6(decoder_1_out6), .out10(decoder_1_out10),
    .out12(decoder_1_out12), .out14(decoder_1_out14), .out15(decoder_1_out15), .sel(FunSel));  // open: out0, out1, out2, out3, out7, out8, out9, out11, out13
  Hex_Digit_Display hex_digit_display_2 (.value(A[3:0]));  // open: dp
  assign not_1_out = ~A;  // NOT_Gate not_1, 8 bits wide
  assign not_2_out = ~B;  // NOT_Gate not_2, 8 bits wide
  Hex_Digit_Display hex_digit_display_3 (.value(OutALU[3:0]));  // open: dp
  Hex_Digit_Display hex_digit_display_4 (.value(OutALU[7:4]));  // open: dp
  arithmetic_shift arithmetic_shift_1 (
    .in_2(FunSel[0]), .A(A), .Output(arithmetic_shift_1_output), .Overflow(arithmetic_shift_1_overflow));
  logical logical_1 (.A(A), .B(B), .AND(logical_1_and), .OR(logical_1_or), .XOR(logical_1_xor));
  arithmetic arithmetic_1 (
    .SEL(FunSel[1:0]), .CIN(Cin), .A(A), .B(B), .OUTPUT(arithmetic_1_output), .COUT(arithmetic_1_cout),
    .OVERFLOW(arithmetic_1_overflow));
  logic_shift logic_shift_1 (.in_2(FunSel[0]), .Carry(logic_shift_1_carry), .A(A), .Output(logic_shift_1_output));
  Multiplexer #(.select(4), .width(8), .enable("false")) multiplexer_1 (
    .in0(A), .in1(B), .in2(not_1_out), .in3(not_2_out), .in4(arithmetic_1_output), .in5(arithmetic_1_output),
    .in6(arithmetic_1_output), .in7(logical_1_and), .in8(logical_1_or), .in9(logical_1_xor),
    .in10(logic_shift_1_output), .in11(logic_shift_1_output), .in12(arithmetic_shift_1_output),
    .in13(arithmetic_shift_1_output), .in14(circular_shift_1_output), .in15(circular_shift_1_output),
    .out(OutALU), .sel(FunSel));
  or or_1 (or_1_out, decoder_1_out4, decoder_1_out5, decoder_1_out6, decoder_1_out12, decoder_1_out14, decoder_1_out15);
  or or_2 (or_2_out, decoder_1_out4, decoder_1_out5, decoder_1_out6, decoder_1_out10, decoder_1_out14, decoder_1_out15);
  circular_shift circular_shift_1 (
    .Cin(Cin), .funsel(FunSel[0]), .Cout(circular_shift_1_cout), .A(A), .Output(circular_shift_1_output),
    .Overflow(circular_shift_1_overflow));
  Hex_Digit_Display hex_digit_display_5 (.value(B[3:0]));  // open: dp
  Hex_Digit_Display hex_digit_display_6 (.value(B[7:4]));  // open: dp
  Multiplexer #(.select(2), .enable("false")) multiplexer_2 (
    .in0(arithmetic_1_cout), .in1(arithmetic_1_cout), .in2(logic_shift_1_carry), .in3(circular_shift_1_cout),
    .out(multiplexer_2_out), .sel(FunSel[3:2]));
  Multiplexer #(.select(3), .enable("false")) multiplexer_3 (
    .in0(1'b1), .in1(1'b1), .in2(arithmetic_1_overflow), .in3(arithmetic_1_overflow), .in4(1'b1), .in5(1'b1),
    .in6(arithmetic_shift_1_overflow), .in7(circular_shift_1_overflow), .out(multiplexer_3_out),
    .sel(FunSel[3:1]));
  not not_3 (not_3_out, or_3_out);
  or or_3 (or_3_out, OutALU[0], OutALU[1], OutALU[2], OutALU[3], OutALU[5], OutALU[6], OutALU[7], OutALU[4]);
  not not_4 (not_4_out, decoder_1_out12);
  xor xor_1 (xor_1_out, OutALU[7], 1'b0);
  buf buffer_1 (OutFlag[3], not_3_out);
  assign OutFlag[2] = or_2_out ? multiplexer_2_out : 1'bz;  // Controlled_Buffer controlled_buffer_1
  assign OutFlag[1] = not_4_out ? xor_1_out : 1'bz;  // Controlled_Buffer controlled_buffer_2
  assign OutFlag[0] = or_1_out ? multiplexer_3_out : 1'bz;  // Controlled_Buffer controlled_buffer_3

  // Notes on the sheet:
  //   carry
  //   overflow
endmodule

module arithmetic (
  input  [7:0] A,
  input  [7:0] B,
  input  CIN,
  input  [1:0] SEL,
  output [7:0] OUTPUT,
  output COUT,
  output OVERFLOW
);

  wire and_1_out, and_2_out, multiplexer_2_out, not_2_out, not_3_out, xor_1_out, xor_2_out, xor_3_out,
       xor_4_out;
  wire [7:0] multiplexer_1_out, not_1_out;

  Multiplexer #(.width(8), .enable("false")) multiplexer_1 (
    .in0(B), .in1(not_1_out), .out(multiplexer_1_out), .sel(SEL[1]));
  assign not_1_out = ~B;  // NOT_Gate not_1, 8 bits wide
  Multiplexer #(.select(2), .enable("false")) multiplexer_2 (
    .in0(1'b0), .in1(CIN), .in2(1'b1), .out(multiplexer_2_out), .sel(SEL));  // open: in3
  Adder adder_1 (.a(A), .b(multiplexer_1_out), .out(OUTPUT), .cin(multiplexer_2_out), .cout(COUT));
  xor xor_1 (xor_1_out, B[7], A[7]);
  xor xor_2 (xor_2_out, not_1_out[7], A[7]);
  not not_2 (not_2_out, xor_1_out);
  not not_3 (not_3_out, xor_2_out);
  xor xor_3 (xor_3_out, OUTPUT[7], B[7]);
  xor xor_4 (xor_4_out, OUTPUT[7], not_1_out[7]);
  and and_1 (and_1_out, xor_3_out, not_2_out);
  and and_2 (and_2_out, xor_4_out, not_3_out);
  Multiplexer #(.enable("false")) multiplexer_3 (.in0(and_1_out), .in1(and_2_out), .out(OVERFLOW), .sel(SEL[1]));
endmodule

module logical (
  input  [7:0] A,
  input  [7:0] B,
  output [7:0] AND,
  output [7:0] OR,
  output [7:0] XOR
);

  assign AND = A & B;  // AND_Gate and_1, 8 bits wide
  assign OR = A | B;  // OR_Gate or_1, 8 bits wide
  assign XOR = A ^ B;  // XOR_Gate xor_1, 8 bits wide
endmodule

module logic_shift (
  input  [7:0] A,
  input  in_2,
  output [7:0] Output,
  output Carry
);

  Multiplexer #(.enable("false")) multiplexer_1 (.in0(1'b0), .in1(A[1]), .out(Output[0]), .sel(in_2));
  Multiplexer #(.enable("false")) multiplexer_2 (.in0(A[0]), .in1(A[2]), .out(Output[1]), .sel(in_2));
  Multiplexer #(.enable("false")) multiplexer_3 (.in0(A[1]), .in1(A[3]), .out(Output[2]), .sel(in_2));
  Multiplexer #(.enable("false")) multiplexer_4 (.in0(A[2]), .in1(A[4]), .out(Output[3]), .sel(in_2));
  Multiplexer #(.enable("false")) multiplexer_5 (.in0(A[3]), .in1(A[5]), .out(Output[4]), .sel(in_2));
  Multiplexer #(.enable("false")) multiplexer_6 (.in0(A[4]), .in1(A[6]), .out(Output[5]), .sel(in_2));
  Multiplexer #(.enable("false")) multiplexer_7 (.in0(A[5]), .in1(A[7]), .out(Output[6]), .sel(in_2));
  Multiplexer #(.enable("false")) multiplexer_8 (.in0(A[6]), .in1(1'b0), .out(Output[7]), .sel(in_2));
  Multiplexer #(.enable("false")) multiplexer_9 (.in0(A[7]), .in1(A[0]), .out(Carry), .sel(in_2));
endmodule

module arithmetic_shift (
  input  [7:0] A,
  input  in_2,
  output [7:0] Output,
  output Overflow
);

  Multiplexer #(.enable("false")) multiplexer_1 (.in0(1'b0), .in1(A[1]), .out(Output[0]), .sel(in_2));
  Multiplexer #(.enable("false")) multiplexer_2 (.in0(A[0]), .in1(A[2]), .out(Output[1]), .sel(in_2));
  Multiplexer #(.enable("false")) multiplexer_3 (.in0(A[1]), .in1(A[3]), .out(Output[2]), .sel(in_2));
  Multiplexer #(.enable("false")) multiplexer_4 (.in0(A[2]), .in1(A[4]), .out(Output[3]), .sel(in_2));
  Multiplexer #(.enable("false")) multiplexer_5 (.in0(A[3]), .in1(A[5]), .out(Output[4]), .sel(in_2));
  Multiplexer #(.enable("false")) multiplexer_6 (.in0(A[4]), .in1(A[6]), .out(Output[5]), .sel(in_2));
  Multiplexer #(.enable("false")) multiplexer_7 (.in0(A[5]), .in1(A[7]), .out(Output[6]), .sel(in_2));
  Multiplexer #(.enable("false")) multiplexer_8 (.in0(A[6]), .in1(A[7]), .out(Output[7]), .sel(in_2));
  xor xor_1 (Overflow, A[6], A[7]);
endmodule

module circular_shift (
  input  Cin,
  input  [7:0] A,
  input  funsel,
  output [7:0] Output,
  output Overflow,
  output Cout
);

  wire xor_1_out, xor_2_out;

  Multiplexer #(.enable("false")) multiplexer_1 (.in0(Cin), .in1(A[1]), .out(Output[0]), .sel(funsel));
  Multiplexer #(.enable("false")) multiplexer_2 (.in0(A[0]), .in1(A[2]), .out(Output[1]), .sel(funsel));
  Multiplexer #(.enable("false")) multiplexer_3 (.in0(A[1]), .in1(A[3]), .out(Output[2]), .sel(funsel));
  Multiplexer #(.enable("false")) multiplexer_4 (.in0(A[2]), .in1(A[4]), .out(Output[3]), .sel(funsel));
  Multiplexer #(.enable("false")) multiplexer_5 (.in0(A[3]), .in1(A[5]), .out(Output[4]), .sel(funsel));
  Multiplexer #(.enable("false")) multiplexer_6 (.in0(A[4]), .in1(A[6]), .out(Output[5]), .sel(funsel));
  Multiplexer #(.enable("false")) multiplexer_7 (.in0(A[5]), .in1(A[7]), .out(Output[6]), .sel(funsel));
  Multiplexer #(.enable("false")) multiplexer_8 (.in0(A[6]), .in1(Cin), .out(Output[7]), .sel(funsel));
  Multiplexer #(.enable("false")) multiplexer_9 (.in0(A[7]), .in1(A[0]), .out(Cout), .sel(funsel));
  xor xor_1 (xor_1_out, A[6], A[7]);
  xor xor_2 (xor_2_out, A[7], Cin);
  Multiplexer #(.enable("false")) multiplexer_10 (.in0(xor_1_out), .in1(xor_2_out), .out(Overflow), .sel(funsel));
endmodule

module Main (
  input  [7:0] A,
  input  [7:0] B,
  input  [3:0] FunSel,
  output [3:0] ZCNO,
  output [7:0] OutALU
);

  wire clock_1_out;
  wire [3:0] alu_1_outflag;

  ALU alu_1 (.FunSel(FunSel), .A(A), .B(B), .OutALU(OutALU), .OutFlag(alu_1_outflag), .Cin(ZCNO[2]));
  Clock clock_1 (.out(clock_1_out));
  register Flag_Register (.CLK(clock_1_out), .out_3(ZCNO), .in_2(alu_1_outflag));
  Hex_Digit_Display hex_digit_display_1 (.value(A[3:0]));  // open: dp
  Hex_Digit_Display hex_digit_display_2 (.value(A[7:4]));  // open: dp
  Hex_Digit_Display hex_digit_display_3 (.value(B[7:4]));  // open: dp
  Hex_Digit_Display hex_digit_display_4 (.value(B[3:0]));  // open: dp
  Hex_Digit_Display hex_digit_display_5 (.value(OutALU[3:0]));  // open: dp
  Hex_Digit_Display hex_digit_display_6 (.value(OutALU[7:4]));  // open: dp
endmodule

module register (
  input  CLK,
  input  [3:0] in_2,
  output [3:0] out_3
);

  D_Flip_Flop d_ff_1 (.clk(CLK), .D(in_2[3]), .Q(out_3[3]));  // open: Qn, preset, en, reset
  D_Flip_Flop d_ff_2 (.clk(CLK), .D(in_2[2]), .Q(out_3[2]));  // open: Qn, preset, en, reset
  D_Flip_Flop d_ff_3 (.clk(CLK), .D(in_2[1]), .Q(out_3[1]));  // open: Qn, preset, en, reset
  D_Flip_Flop d_ff_4 (.clk(CLK), .D(in_2[0]), .Q(out_3[0]));  // open: Qn, preset, en, reset
endmodule
